// Logisim project FullCircuit.circ as structural Verilog: 17 circuits, main circuit main
module main (
  input  in_1,
  output [15:0] PortAOut,
  output [15:0] PortBOut,
  output [15:0] out_4,
  output [15:0] AccumulatorValue,
  output [15:0] DataBus,
  output [15:0] out_7
);

  wire clock_1_out, controlunit_1_accallowinp, controlunit_1_accclock, controlunit_1_accumulatorout,
       controlunit_1_clkout, controlunit_1_nclrir, controlunit_1_portaout, controlunit_1_portbout,
       controlunit_1_progmemout, controlunit_1_skip, controlunit_1_statusout, controlunit_1_varmemout,
       controlunit_1_varwrite, jumpmanager_1_pc_jump, jumpmanager_1_pc_return, jumpmanager_1_stack_pop,
       jumpmanager_1_stack_push, n7414_1_pin2, n7414_1_pin12, n74541_1_pin1, not_1_out, not_2_out, not_3_out,
       not_4_out, not_5_out, not_6_out, not_7_out, not_8_out, programcounter_1_endinst, programcounter_1_s0,
       pull_resistor_1_node, pull_resistor_2_node, stack_1_nseterror, statusregister_1_agreatb,
       statusregister_1_aisb, statusregister_1_alessb, statusregister_1_negative, statusregister_1_nerror,
       statusregister_1_overflow, statusregister_1_skip, statusregister_1_underflow, statusregister_1_zero,
       switch_3_p2, switch_4_p2;
  wire [0:0] programcounter_1_s1;
  wire [6:0] alu_1_zero;
  wire [7:0] ram_3_data, ram_4_data, rom_1_data, rom_2_data;
  wire [15:0] ram_1_data, stack_1_stackout;

  Pull_Resistor pull_resistor_1 (.node(pull_resistor_1_node));
  // Switch switch_1: pin names not known; wires that end beside it: 1'b1, pull_resistor_1_node
  Pull_Resistor pull_resistor_2 (.node(pull_resistor_2_node));
  // Switch switch_2: pin names not known; wires that end beside it: 1'b1, pull_resistor_2_node
  _7414 #(.ShowInternalStructure("true")) u_7414_1 (
    .pin1(pull_resistor_2_node), .pin2(n7414_1_pin2), .pin13(pull_resistor_1_node), .pin12(n7414_1_pin12));  // open: pin3, pin4, pin5, pin6, pin11, pin10, pin9, pin8
  JumpManager jumpmanager_1 (
    .S1(programcounter_1_s1[0]), .CLK(controlunit_1_clkout), .InstructionRegister(out_4),
    .PC_Jump(jumpmanager_1_pc_jump), .Stack_Push(jumpmanager_1_stack_push),
    .Stack_Pop(jumpmanager_1_stack_pop), .PC_Return(jumpmanager_1_pc_return));
  ProgramCounter programcounter_1 (
    .DataBusIn(DataBus), .CallJump(jumpmanager_1_pc_jump), .stackReturn(jumpmanager_1_pc_return),
    .CLR(pull_resistor_1_node), .Clk(controlunit_1_clkout), .Skip(statusregister_1_skip),
    .S0(programcounter_1_s0), .S1(programcounter_1_s1[0]), .PCout(out_7), .EndInst(programcounter_1_endinst));
  ROM #(.addrWidth(15)) rom_1 (.addr({out_7[13:0], programcounter_1_s1[0]}), .data(rom_1_data));
  ROM #(.addrWidth(15)) rom_2 (.addr({out_7[13:0], programcounter_1_s1[0]}), .data(rom_2_data));
  InstructionRegister instructionregister_1 (
    .DataBus(DataBus), .clk(programcounter_1_s1[0]), .nClearIR(controlunit_1_nclrir), .DataOut(out_4));
  // Switch switch_3: pin names not known; wires that end beside it: 1'b1, switch_3_p2
  _74541 #(.ShowInternalStructure("true")) u_74541_1 (
    .pin1(n74541_1_pin1), .pin2(stack_1_stackout[8]), .pin3(stack_1_stackout[9]),
    .pin4(stack_1_stackout[10]), .pin5(stack_1_stackout[11]), .pin6(stack_1_stackout[12]),
    .pin7(stack_1_stackout[13]), .pin8(stack_1_stackout[14]), .pin9(stack_1_stackout[15]),
    .pin19(n74541_1_pin1), .pin18(DataBus[8]), .pin17(DataBus[9]), .pin16(DataBus[10]), .pin15(DataBus[11]),
    .pin14(DataBus[12]), .pin13(DataBus[13]), .pin12(DataBus[14]), .pin11(DataBus[15]));
  Pull_Resistor pull_resistor_3 (.node(switch_3_p2));
  // Switch switch_4: pin names not known; wires that end beside it: 1'b0, switch_4_p2
  Stack stack_1 (
    .Push(jumpmanager_1_stack_push), .Pop(jumpmanager_1_stack_pop), .PCin(out_7),
    .nSetError(stack_1_nseterror), .StackOut(stack_1_stackout));
  Pull_Resistor #(.pull(1)) pull_resistor_4 (.node(switch_4_p2));
  Clock clock_1 (.out(clock_1_out));
  _74541 #(.ShowInternalStructure("true")) u_74541_2 (
    .pin1(n74541_1_pin1), .pin2(stack_1_stackout[0]), .pin3(stack_1_stackout[1]), .pin4(stack_1_stackout[2]),
    .pin5(stack_1_stackout[3]), .pin6(stack_1_stackout[4]), .pin7(stack_1_stackout[5]),
    .pin8(stack_1_stackout[6]), .pin9(stack_1_stackout[7]), .pin19(n74541_1_pin1), .pin18(DataBus[0]),
    .pin17(DataBus[1]), .pin16(DataBus[2]), .pin15(DataBus[3]), .pin14(DataBus[4]), .pin13(DataBus[5]),
    .pin12(DataBus[6]), .pin11(DataBus[7]));
  RAM #(.addrWidth(15), .databus("bidir"), .trigger("high")) ram_1 (
    .addr({out_7[13:0], programcounter_1_s1[0]}), .we(not_1_out), .oe(not_2_out), .data(ram_1_data[7:0]));
  not not_1 (not_1_out, n7414_1_pin2);
  not not_2 (not_2_out, pull_resistor_2_node);
  RAM #(.addrWidth(15), .databus("bidir"), .trigger("high")) ram_2 (
    .addr({out_7[13:0], programcounter_1_s1[0]}), .we(not_3_out), .oe(not_4_out), .data(ram_1_data[15:8]));
  not not_3 (not_3_out, n7414_1_pin2);
  not not_4 (not_4_out, pull_resistor_2_node);
  ControlUnit controlunit_1 (
    .nStopHalt(switch_4_p2), .ProgramLoad(pull_resistor_2_node), .clockEnable(switch_3_p2),
    .notError(statusregister_1_nerror), .Clk(clock_1_out), .DataBus(DataBus), .ProgMemIn(ram_1_data),
    .IRin(out_4), .S0(programcounter_1_s0), .S1(programcounter_1_s1[0]), .Load(pull_resistor_2_node),
    .ClkOut(controlunit_1_clkout), .AccClock(controlunit_1_accclock), .Skip(controlunit_1_skip),
    .nClrIR(controlunit_1_nclrir), .VarWrite(controlunit_1_varwrite), .VarMemOut(controlunit_1_varmemout),
    .ProgMemOut(controlunit_1_progmemout), .StackOut(n74541_1_pin1), .StatusOut(controlunit_1_statusout),
    .AccumulatorOut(controlunit_1_accumulatorout), .PortAOut(controlunit_1_portaout),
    .PortBOut(controlunit_1_portbout), .AccAllowInp(controlunit_1_accallowinp));  // open: RisingEdge, FallingEdge, PortCOut, PortDOut
  _74541 #(.ShowInternalStructure("true")) u_74541_3 (
    .pin1(controlunit_1_progmemout), .pin2(ram_1_data[7]), .pin3(ram_1_data[6]), .pin4(ram_1_data[5]),
    .pin5(ram_1_data[4]), .pin6(ram_1_data[3]), .pin7(ram_1_data[2]), .pin8(ram_1_data[1]),
    .pin9(ram_1_data[0]), .pin19(controlunit_1_progmemout), .pin18(DataBus[7]), .pin17(DataBus[6]),
    .pin16(DataBus[5]), .pin15(DataBus[4]), .pin14(DataBus[3]), .pin13(DataBus[2]), .pin12(DataBus[1]),
    .pin11(DataBus[0]));
  _74541 #(.ShowInternalStructure("true")) u_74541_4 (
    .pin1(n7414_1_pin2), .pin2(rom_1_data[7]), .pin3(rom_1_data[6]), .pin4(rom_1_data[5]),
    .pin5(rom_1_data[4]), .pin6(rom_1_data[3]), .pin7(rom_1_data[2]), .pin8(rom_1_data[1]),
    .pin9(rom_1_data[0]), .pin19(n7414_1_pin2), .pin18(ram_1_data[7]), .pin17(ram_1_data[6]),
    .pin16(ram_1_data[5]), .pin15(ram_1_data[4]), .pin14(ram_1_data[3]), .pin13(ram_1_data[2]),
    .pin12(ram_1_data[1]), .pin11(ram_1_data[0]));
  _74541 #(.ShowInternalStructure("true")) u_74541_5 (
    .pin1(controlunit_1_progmemout), .pin2(ram_1_data[15]), .pin3(ram_1_data[14]), .pin4(ram_1_data[13]),
    .pin5(ram_1_data[12]), .pin6(ram_1_data[11]), .pin7(ram_1_data[10]), .pin8(ram_1_data[9]),
    .pin9(ram_1_data[8]), .pin19(controlunit_1_progmemout), .pin18(DataBus[15]), .pin17(DataBus[14]),
    .pin16(DataBus[13]), .pin15(DataBus[12]), .pin14(DataBus[11]), .pin13(DataBus[10]), .pin12(DataBus[9]),
    .pin11(DataBus[8]));
  _74541 #(.ShowInternalStructure("true")) u_74541_6 (
    .pin1(n7414_1_pin2), .pin2(rom_2_data[7]), .pin3(rom_2_data[6]), .pin4(rom_2_data[5]),
    .pin5(rom_2_data[4]), .pin6(rom_2_data[3]), .pin7(rom_2_data[2]), .pin8(rom_2_data[1]),
    .pin9(rom_2_data[0]), .pin19(n7414_1_pin2), .pin18(ram_1_data[15]), .pin17(ram_1_data[14]),
    .pin16(ram_1_data[13]), .pin15(ram_1_data[12]), .pin14(ram_1_data[11]), .pin13(ram_1_data[10]),
    .pin12(ram_1_data[9]), .pin11(ram_1_data[8]));
  StatusRegister statusregister_1 (
    .IgnoreError(in_1), .nSetError(stack_1_nseterror), .SetSkip(controlunit_1_skip),
    .nLoading(pull_resistor_2_node), .S0(programcounter_1_s0), .SetZero(alu_1_zero[0]),
    .SetNegative(alu_1_zero[1]), .SetOverflow(alu_1_zero[2]), .SetUnderflow(alu_1_zero[3]),
    .SetAlessB(alu_1_zero[4]), .SetAisB(alu_1_zero[5]), .SetAgreatB(alu_1_zero[6]),
    .nError(statusregister_1_nerror), .Skip(statusregister_1_skip), .Zero(statusregister_1_zero),
    .Negative(statusregister_1_negative), .Overflow(statusregister_1_overflow),
    .Underflow(statusregister_1_underflow), .AlessB(statusregister_1_alessb), .AisB(statusregister_1_aisb),
    .AgreatB(statusregister_1_agreatb));
  _74541 #(.ShowInternalStructure("true")) u_74541_7 (
    .pin1(controlunit_1_statusout), .pin3(statusregister_1_agreatb), .pin4(statusregister_1_aisb),
    .pin5(statusregister_1_alessb), .pin6(statusregister_1_underflow), .pin7(statusregister_1_overflow),
    .pin8(statusregister_1_negative), .pin9(statusregister_1_zero), .pin19(controlunit_1_statusout),
    .pin17(DataBus[6]), .pin16(DataBus[5]), .pin15(DataBus[4]), .pin14(DataBus[3]), .pin13(DataBus[2]),
    .pin12(DataBus[1]), .pin11(DataBus[0]));  // open: pin2, pin18
  ALU alu_1 (
    .AllowIn(controlunit_1_accallowinp), .AllowOut(controlunit_1_accumulatorout),
    .AccumulatorClock(controlunit_1_accclock), .IR4t0(out_4[4:0]), .DataBusIn(DataBus),
    .EndInst(programcounter_1_endinst), .nClearAccumulator(n7414_1_pin12), .AccumulatorBus(DataBus),
    .AccumulatorOut(AccumulatorValue), .Zero(alu_1_zero[0]), .Negative(alu_1_zero[1]),
    .Overflow(alu_1_zero[2]), .Underflow(alu_1_zero[3]), .AlessB(alu_1_zero[4]), .AisB(alu_1_zero[5]),
    .AgreatB(alu_1_zero[6]));
  RAM #(.addrWidth(15), .databus("bidir"), .trigger("high")) ram_3 (
    .addr(ram_1_data[14:0]), .we(not_5_out), .oe(not_6_out), .data(ram_3_data));
  not not_5 (not_5_out, controlunit_1_varwrite);
  not not_6 (not_6_out, controlunit_1_varmemout);
  RAM #(.addrWidth(15), .databus("bidir"), .trigger("high")) ram_4 (
    .addr(ram_1_data[14:0]), .we(not_7_out), .oe(not_8_out), .data(ram_4_data));
  not not_7 (not_7_out, controlunit_1_varwrite);
  not not_8 (not_8_out, controlunit_1_varmemout);
  OutputPortA outputporta_1 (
    .DataBus(DataBus), .InstructionRegister(out_4), .S1(programcounter_1_s1[0]),
    .Clock(controlunit_1_clkout), .PortOutput(PortAOut));
  OutputPortB outputportb_1 (
    .DataBus(DataBus), .InstructionRegister(out_4), .S1(programcounter_1_s1[0]),
    .Clock(controlunit_1_clkout), .PortOutput(PortBOut));
  _74541 #(.ShowInternalStructure("true")) u_74541_8 (
    .pin1(controlunit_1_varmemout), .pin2(ram_3_data[7]), .pin3(ram_3_data[6]), .pin4(ram_3_data[5]),
    .pin5(ram_3_data[4]), .pin6(ram_3_data[3]), .pin7(ram_3_data[2]), .pin8(ram_3_data[1]),
    .pin9(ram_3_data[0]), .pin19(controlunit_1_varmemout), .pin18(DataBus[7]), .pin17(DataBus[6]),
    .pin16(DataBus[5]), .pin15(DataBus[4]), .pin14(DataBus[3]), .pin13(DataBus[2]), .pin12(DataBus[1]),
    .pin11(DataBus[0]));
  _74541 #(.ShowInternalStructure("true")) u_74541_9 (
    .pin1(controlunit_1_varwrite), .pin2(AccumulatorValue[15]), .pin3(AccumulatorValue[14]),
    .pin4(AccumulatorValue[13]), .pin5(AccumulatorValue[12]), .pin6(AccumulatorValue[11]),
    .pin7(AccumulatorValue[10]), .pin8(AccumulatorValue[9]), .pin9(AccumulatorValue[8]),
    .pin19(controlunit_1_varwrite), .pin18(ram_3_data[7]), .pin17(ram_3_data[6]), .pin16(ram_3_data[5]),
    .pin15(ram_3_data[4]), .pin14(ram_3_data[3]), .pin13(ram_3_data[2]), .pin12(ram_3_data[1]),
    .pin11(ram_3_data[0]));
  _74541 #(.ShowInternalStructure("true")) u_74541_10 (
    .pin1(controlunit_1_portbout), .pin2(PortBOut[8]), .pin3(PortBOut[9]), .pin4(PortBOut[10]),
    .pin5(PortBOut[11]), .pin6(PortBOut[12]), .pin7(PortBOut[13]), .pin8(PortBOut[14]), .pin9(PortBOut[15]),
    .pin19(controlunit_1_portbout), .pin18(DataBus[8]), .pin17(DataBus[9]), .pin16(DataBus[10]),
    .pin15(DataBus[11]), .pin14(DataBus[12]), .pin13(DataBus[13]), .pin12(DataBus[14]), .pin11(DataBus[15]));
  _74541 #(.ShowInternalStructure("true")) u_74541_11 (
    .pin1(controlunit_1_portaout), .pin2(PortAOut[8]), .pin3(PortAOut[9]), .pin4(PortAOut[10]),
    .pin5(PortAOut[11]), .pin6(PortAOut[12]), .pin7(PortAOut[13]), .pin8(PortAOut[14]), .pin9(PortAOut[15]),
    .pin19(controlunit_1_portaout), .pin18(DataBus[8]), .pin17(DataBus[9]), .pin16(DataBus[10]),
    .pin15(DataBus[11]), .pin14(DataBus[12]), .pin13(DataBus[13]), .pin12(DataBus[14]), .pin11(DataBus[15]));
  _74541 #(.ShowInternalStructure("true")) u_74541_12 (
    .pin1(controlunit_1_varmemout), .pin2(ram_4_data[7]), .pin3(ram_4_data[6]), .pin4(ram_4_data[5]),
    .pin5(ram_4_data[4]), .pin6(ram_4_data[3]), .pin7(ram_4_data[2]), .pin8(ram_4_data[1]),
    .pin9(ram_4_data[0]), .pin19(controlunit_1_varmemout), .pin18(DataBus[15]), .pin17(DataBus[14]),
    .pin16(DataBus[13]), .pin15(DataBus[12]), .pin14(DataBus[11]), .pin13(DataBus[10]), .pin12(DataBus[9]),
    .pin11(DataBus[8]));
  _74541 #(.ShowInternalStructure("true")) u_74541_13 (
    .pin1(controlunit_1_varwrite), .pin2(AccumulatorValue[7]), .pin3(AccumulatorValue[6]),
    .pin4(AccumulatorValue[5]), .pin5(AccumulatorValue[4]), .pin6(AccumulatorValue[3]),
    .pin7(AccumulatorValue[2]), .pin8(AccumulatorValue[1]), .pin9(AccumulatorValue[0]),
    .pin19(controlunit_1_varwrite), .pin18(ram_4_data[7]), .pin17(ram_4_data[6]), .pin16(ram_4_data[5]),
    .pin15(ram_4_data[4]), .pin14(ram_4_data[3]), .pin13(ram_4_data[2]), .pin12(ram_4_data[1]),
    .pin11(ram_4_data[0]));
  _74541 #(.ShowInternalStructure("true")) u_74541_14 (
    .pin1(controlunit_1_portaout), .pin2(PortAOut[0]), .pin3(PortAOut[1]), .pin4(PortAOut[2]),
    .pin5(PortAOut[3]), .pin6(PortAOut[4]), .pin7(PortAOut[5]), .pin8(PortAOut[6]), .pin9(PortAOut[7]),
    .pin19(controlunit_1_portaout), .pin18(DataBus[0]), .pin17(DataBus[1]), .pin16(DataBus[2]),
    .pin15(DataBus[3]), .pin14(DataBus[4]), .pin13(DataBus[5]), .pin12(DataBus[6]), .pin11(DataBus[7]));
  _74541 #(.ShowInternalStructure("true")) u_74541_15 (
    .pin1(controlunit_1_portbout), .pin2(PortBOut[0]), .pin3(PortBOut[1]), .pin4(PortBOut[2]),
    .pin5(PortBOut[3]), .pin6(PortBOut[4]), .pin7(PortBOut[5]), .pin8(PortBOut[6]), .pin9(PortBOut[7]),
    .pin19(controlunit_1_portbout), .pin18(DataBus[0]), .pin17(DataBus[1]), .pin16(DataBus[2]),
    .pin15(DataBus[3]), .pin14(DataBus[4]), .pin13(DataBus[5]), .pin12(DataBus[6]), .pin11(DataBus[7]));

  // Notes on the sheet:
  //   Load Program
  //   Reset
  //   contents of rom_1 (hex, n*v repeats v):
  //   4 34 5 1 4*0 6
  //   contents of rom_2 (hex, n*v repeats v):
  //   84 12 22
  //   Clock Enable
  //   ROM
  //   Stop Halt
  //   ProgramMemory
  //   VariableMemory
endmodule

module x16bitComparitor (
  input  [15:0] Ain,
  input  [15:0] Bin,
  input  Power,
  output AisB,
  output AlessB,
  output AgreaterB
);

  wire n7408_1_pin3, n7408_1_pin6, n7408_1_pin7, n7408_1_pin11, n7408_2_pin3, n7408_2_pin6, n7408_2_pin7,
       n7408_3_pin3, n7408_3_pin6, n7408_3_pin7, n7432_1_pin3, n7432_1_pin6, n7432_1_pin7, n7432_2_pin3,
       n7432_2_pin6, n7432_2_pin7, n7432_3_pin7, n7485_1_pin2, n7485_1_pin3, n7485_1_pin5, n7485_1_pin6,
       n7485_1_pin7, n7485_1_pin8, n7485_2_pin5, n7485_2_pin6, n7485_2_pin7, n7485_2_pin8, n7485_3_pin2,
       n7485_3_pin3, n7485_3_pin5, n7485_3_pin6, n7485_3_pin7, n7485_3_pin8, n7485_4_pin5, n7485_4_pin6,
       n7485_4_pin7, n7485_4_pin8;

  _7485 #(.ShowInternalStructure("true"), .VccGndPorts("true")) u_7485_1 (
    .pin1(Bin[11]), .pin2(n7485_1_pin2), .pin3(n7485_1_pin3), .pin4(n7485_1_pin2), .pin5(n7485_1_pin5),
    .pin6(n7485_1_pin6), .pin7(n7485_1_pin7), .pin8(n7485_1_pin8), .pin16(Power), .pin15(Ain[11]),
    .pin14(Bin[10]), .pin13(Ain[10]), .pin12(Ain[9]), .pin11(Bin[9]), .pin10(Ain[8]), .pin9(Bin[8]));
  _7485 #(.ShowInternalStructure("true"), .VccGndPorts("true")) u_7485_2 (
    .pin1(Bin[15]), .pin2(n7485_1_pin2), .pin3(n7485_1_pin3), .pin4(n7485_1_pin2), .pin5(n7485_2_pin5),
    .pin6(n7485_2_pin6), .pin7(n7485_2_pin7), .pin8(n7485_2_pin8), .pin16(Power), .pin15(Ain[15]),
    .pin14(Bin[14]), .pin13(Ain[14]), .pin12(Ain[13]), .pin11(Bin[13]), .pin10(Ain[12]), .pin9(Bin[12]));
  _7485 #(.ShowInternalStructure("true"), .VccGndPorts("true")) u_7485_3 (
    .pin1(Bin[3]), .pin2(n7485_3_pin2), .pin3(n7485_3_pin3), .pin4(n7485_3_pin2), .pin5(n7485_3_pin5),
    .pin6(n7485_3_pin6), .pin7(n7485_3_pin7), .pin8(n7485_3_pin8), .pin16(Power), .pin15(Ain[3]),
    .pin14(Bin[2]), .pin13(Ain[2]), .pin12(Ain[1]), .pin11(Bin[1]), .pin10(Ain[0]), .pin9(Bin[0]));
  _7485 #(.ShowInternalStructure("true"), .VccGndPorts("true")) u_7485_4 (
    .pin1(Bin[7]), .pin2(n7485_3_pin2), .pin3(n7485_3_pin3), .pin4(n7485_3_pin2), .pin5(n7485_4_pin5),
    .pin6(n7485_4_pin6), .pin7(n7485_4_pin7), .pin8(n7485_4_pin8), .pin16(Power), .pin15(Ain[7]),
    .pin14(Bin[6]), .pin13(Ain[6]), .pin12(Ain[5]), .pin11(Bin[5]), .pin10(Ain[4]), .pin9(Bin[4]));
  _7408 #(.ShowInternalStructure("true"), .VccGndPorts("true")) u_7408_1 (
    .pin1(n7485_2_pin6), .pin2(n7485_1_pin7), .pin3(n7408_1_pin3), .pin4(n7485_2_pin6), .pin5(n7485_1_pin5),
    .pin6(n7408_1_pin6), .pin7(n7408_1_pin7), .pin14(Power), .pin13(n7485_2_pin6), .pin12(n7485_1_pin6),
    .pin11(n7408_1_pin11));  // open: pin10, pin9, pin8
  _7408 #(.ShowInternalStructure("true"), .VccGndPorts("true")) u_7408_2 (
    .pin1(n7485_4_pin6), .pin2(n7485_3_pin7), .pin3(n7408_2_pin3), .pin4(n7485_4_pin6), .pin5(n7485_3_pin5),
    .pin6(n7408_2_pin6), .pin7(n7408_2_pin7), .pin14(Power), .pin13(n7485_4_pin6), .pin12(n7485_3_pin6),
    .pin11(n7408_1_pin11));  // open: pin10, pin9, pin8
  _7432 #(.ShowInternalStructure("true"), .VccGndPorts("true")) u_7432_1 (
    .pin1(n7408_1_pin3), .pin2(n7485_2_pin7), .pin3(n7432_1_pin3), .pin4(n7408_1_pin6), .pin5(n7485_2_pin5),
    .pin6(n7432_1_pin6), .pin7(n7432_1_pin7), .pin14(Power));  // open: pin13, pin12, pin11, pin10, pin9, pin8
  _7432 #(.ShowInternalStructure("true"), .VccGndPorts("true")) u_7432_2 (
    .pin1(n7408_2_pin3), .pin2(n7485_4_pin7), .pin3(n7432_2_pin3), .pin4(n7408_2_pin6), .pin5(n7485_4_pin5),
    .pin6(n7432_2_pin6), .pin7(n7432_2_pin7), .pin14(Power));  // open: pin13, pin12, pin11, pin10, pin9, pin8
  _7408 #(.ShowInternalStructure("true"), .VccGndPorts("true")) u_7408_3 (
    .pin1(n7408_1_pin11), .pin2(n7432_2_pin3), .pin3(n7408_3_pin3), .pin4(n7408_1_pin11),
    .pin5(n7432_2_pin6), .pin6(n7408_3_pin6), .pin7(n7408_3_pin7), .pin14(Power), .pin13(n7408_1_pin11),
    .pin12(n7408_1_pin11), .pin11(AisB));  // open: pin10, pin9, pin8
  _7432 #(.ShowInternalStructure("true"), .VccGndPorts("true")) u_7432_3 (
    .pin1(n7408_3_pin3), .pin2(n7432_1_pin3), .pin3(AlessB), .pin4(n7408_3_pin6), .pin5(n7432_1_pin6),
    .pin6(AgreaterB), .pin7(n7432_3_pin7), .pin14(Power));  // open: pin13, pin12, pin11, pin10, pin9, pin8
  // also tied to GND on the sheet: {n7485_1_pin2, n7485_3_pin2, n7485_1_pin8, n7485_2_pin8, n7485_3_pin8, n7485_4_pin8, n7408_1_pin7, n7408_2_pin7, n7432_1_pin7, n7432_2_pin7, n7408_3_pin7, n7432_3_pin7}
  // also tied to VCC on the sheet: {n7485_1_pin3, n7485_3_pin3}
endmodule

module ShiftHandler (
  input  RLF,
  input  [15:0] Ain,
  input  Power,
  output nUF,
  output nOF,
  output [15:0] ShiftOut
);

  wire n7400_1_pin3, n7400_1_pin7, n74157_1_pin3, n74157_1_pin15, n74157_2_pin15, n74157_3_pin15,
       n74157_4_pin14, n74157_4_pin15;

  _7400 #(.ShowInternalStructure("true"), .VccGndPorts("true")) u_7400_1 (
    .pin1(RLF), .pin2(RLF), .pin3(n7400_1_pin3), .pin4(n7400_1_pin3), .pin5(Ain[0]), .pin6(nUF),
    .pin7(n7400_1_pin7), .pin14(Power), .pin13(n7400_1_pin3), .pin12(Ain[15]), .pin11(nOF));  // open: pin10, pin9, pin8
  _74157 #(.ShowInternalStructure("true"), .VccGndPorts("true")) u_74157_1 (
    .pin1(RLF), .pin2(Ain[1]), .pin3(n74157_1_pin3), .pin4(ShiftOut[0]), .pin5(Ain[2]), .pin6(Ain[0]),
    .pin7(ShiftOut[1]), .pin8(n7400_1_pin7), .pin16(Power), .pin15(n74157_1_pin15), .pin14(Ain[4]),
    .pin13(Ain[2]), .pin12(ShiftOut[3]), .pin11(Ain[3]), .pin10(Ain[1]), .pin9(ShiftOut[2]));
  _74157 #(.ShowInternalStructure("true"), .VccGndPorts("true")) u_74157_2 (
    .pin1(RLF), .pin2(Ain[5]), .pin3(Ain[3]), .pin4(ShiftOut[4]), .pin5(Ain[6]), .pin6(Ain[4]),
    .pin7(ShiftOut[5]), .pin8(n7400_1_pin7), .pin16(Power), .pin15(n74157_2_pin15), .pin14(Ain[8]),
    .pin13(Ain[6]), .pin12(ShiftOut[7]), .pin11(Ain[7]), .pin10(Ain[5]), .pin9(ShiftOut[6]));
  _74157 #(.ShowInternalStructure("true"), .VccGndPorts("true")) u_74157_3 (
    .pin1(RLF), .pin2(Ain[9]), .pin3(Ain[7]), .pin4(ShiftOut[8]), .pin5(Ain[10]), .pin6(Ain[8]),
    .pin7(ShiftOut[9]), .pin8(n7400_1_pin7), .pin16(Power), .pin15(n74157_3_pin15), .pin14(Ain[12]),
    .pin13(Ain[10]), .pin12(ShiftOut[11]), .pin11(Ain[11]), .pin10(Ain[9]), .pin9(ShiftOut[10]));
  _74157 #(.ShowInternalStructure("true"), .VccGndPorts("true")) u_74157_4 (
    .pin1(RLF), .pin2(Ain[13]), .pin3(Ain[11]), .pin4(ShiftOut[12]), .pin5(Ain[14]), .pin6(Ain[12]),
    .pin7(ShiftOut[13]), .pin8(n7400_1_pin7), .pin16(Power), .pin15(n74157_4_pin15), .pin14(n74157_4_pin14),
    .pin13(Ain[14]), .pin12(ShiftOut[15]), .pin11(Ain[15]), .pin10(Ain[13]), .pin9(ShiftOut[14]));
  // also tied to GND on the sheet: {n74157_1_pin15, n74157_1_pin3, n74157_2_pin15, n7400_1_pin7, n74157_3_pin15, n74157_4_pin15, n74157_4_pin14}
endmodule

module Accumulator (
  input  [15:0] DataIn,
  input  Clock,
  input  nClear,
  output [15:0] DataOut,
  output Zero,
  output Neg
);

  wire n7432_1_pin3, n7432_1_pin6, n7432_1_pin8, n7432_1_pin11, n7432_2_pin3, n7432_2_pin6, n7432_2_pin8,
       n7432_2_pin11, n7432_3_pin3, n7432_3_pin6, n7432_3_pin8, n7432_3_pin11, n7432_4_pin3, n7432_4_pin11;

  _74273 #(.ShowInternalStructure("true")) u_74273_1 (
    .pin1(nClear), .pin2(DataOut[8]), .pin3(DataIn[8]), .pin4(DataIn[9]), .pin5(DataOut[9]),
    .pin6(DataOut[10]), .pin7(DataIn[10]), .pin8(DataIn[11]), .pin9(DataOut[11]), .pin19(DataOut[15]),
    .pin18(DataIn[15]), .pin17(DataIn[14]), .pin16(DataOut[14]), .pin15(DataOut[13]), .pin14(DataIn[13]),
    .pin13(DataIn[12]), .pin12(DataOut[12]), .pin11(Clock));
  _74273 #(.ShowInternalStructure("true")) u_74273_2 (
    .pin1(nClear), .pin2(DataOut[0]), .pin3(DataIn[0]), .pin4(DataIn[1]), .pin5(DataOut[1]),
    .pin6(DataOut[2]), .pin7(DataIn[2]), .pin8(DataIn[3]), .pin9(DataOut[3]), .pin19(DataOut[7]),
    .pin18(DataIn[7]), .pin17(DataIn[6]), .pin16(DataOut[6]), .pin15(DataOut[5]), .pin14(DataIn[5]),
    .pin13(DataIn[4]), .pin12(DataOut[4]), .pin11(Clock));
  _7432 #(.ShowInternalStructure("true")) u_7432_1 (
    .pin1(DataOut[11]), .pin2(DataOut[10]), .pin3(n7432_1_pin3), .pin4(DataOut[9]), .pin5(DataOut[8]),
    .pin6(n7432_1_pin6), .pin13(DataOut[12]), .pin12(DataOut[13]), .pin11(n7432_1_pin11),
    .pin10(DataOut[14]), .pin9(DataOut[15]), .pin8(n7432_1_pin8));
  _7432 #(.ShowInternalStructure("true")) u_7432_2 (
    .pin1(n7432_1_pin6), .pin2(n7432_1_pin3), .pin3(n7432_2_pin3), .pin4(DataOut[3]), .pin5(DataOut[2]),
    .pin6(n7432_2_pin6), .pin13(n7432_1_pin8), .pin12(n7432_1_pin11), .pin11(n7432_2_pin11),
    .pin10(DataOut[4]), .pin9(DataOut[5]), .pin8(n7432_2_pin8));
  _7432 #(.ShowInternalStructure("true")) u_7432_3 (
    .pin1(DataOut[1]), .pin2(DataOut[0]), .pin3(n7432_3_pin3), .pin4(n7432_3_pin3), .pin5(n7432_2_pin6),
    .pin6(n7432_3_pin6), .pin13(DataOut[6]), .pin12(DataOut[7]), .pin11(n7432_3_pin11),
    .pin10(n7432_3_pin11), .pin9(n7432_2_pin8), .pin8(n7432_3_pin8));
  _7432 #(.ShowInternalStructure("true")) u_7432_4 (
    .pin1(n7432_3_pin6), .pin2(n7432_2_pin3), .pin3(n7432_4_pin3), .pin13(n7432_3_pin8),
    .pin12(n7432_2_pin11), .pin11(n7432_4_pin11));  // open: pin4, pin5, pin6, pin10, pin9, pin8
  _7402 #(.ShowInternalStructure("true")) u_7402_1 (
    .pin1(Zero), .pin2(n7432_4_pin11), .pin3(n7432_4_pin3));  // open: pin4, pin5, pin6, pin13, pin12, pin11, pin10, pin9, pin8

  assign Neg = DataOut[15];
endmodule

module InputPort (
  input  In0,
  input  In1,
  input  In2,
  input  In3,
  input  In4,
  input  In5,
  input  In6,
  input  In7,
  input  In8,
  input  In9,
  input  In10,
  input  In11,
  input  In12,
  input  In13,
  input  In14,
  input  In15,
  output Q0,
  output nQ0,
  output Q1,
  output nQ1,
  output Q2,
  output nQ2,
  output Q3,
  output nQ3,
  output Q4,
  output nQ4,
  output Q5,
  output nQ5,
  output Q6,
  output nQ6,
  output Q7,
  output nQ7,
  output Q8,
  output nQ8,
  output Q9,
  output nQ9,
  output Q10,
  output nQ10,
  output Q11,
  output nQ11,
  output Q12,
  output nQ12,
  output Q13,
  output nQ13,
  output Q14,
  output nQ14,
  output Q15,
  output nQ15
);

  wire n7414_1_pin2, n7414_1_pin4, n7414_1_pin6, n7414_1_pin8, n7414_1_pin10, n7414_1_pin12, n7414_2_pin2,
       n7414_2_pin4, n7414_2_pin6, n7414_2_pin8, n7414_2_pin10, n7414_2_pin12, n7414_3_pin2, n7414_3_pin4,
       n7414_3_pin10, n7414_3_pin12;

  _7414 #(.ShowInternalStructure("true")) u_7414_1 (
    .pin1(In0), .pin2(n7414_1_pin2), .pin3(In1), .pin4(n7414_1_pin4), .pin5(In2), .pin6(n7414_1_pin6),
    .pin13(In3), .pin12(n7414_1_pin12), .pin11(In4), .pin10(n7414_1_pin10), .pin9(In5), .pin8(n7414_1_pin8));
  _7414 #(.ShowInternalStructure("true")) u_7414_2 (
    .pin1(In6), .pin2(n7414_2_pin2), .pin3(In7), .pin4(n7414_2_pin4), .pin5(In8), .pin6(n7414_2_pin6),
    .pin13(In9), .pin12(n7414_2_pin12), .pin11(In10), .pin10(n7414_2_pin10), .pin9(In11), .pin8(n7414_2_pin8));
  _7414 #(.ShowInternalStructure("true")) u_7414_3 (
    .pin1(In12), .pin2(n7414_3_pin2), .pin3(In13), .pin4(n7414_3_pin4), .pin13(In14), .pin12(n7414_3_pin12),
    .pin11(In15), .pin10(n7414_3_pin10));  // open: pin5, pin6, pin9, pin8
  _7474 #(.ShowInternalStructure("true")) u_7474_1 (
    .pin1(In0), .pin4(n7414_1_pin2), .pin5(Q0), .pin6(nQ0), .pin13(In3), .pin10(n7414_1_pin12), .pin9(Q3),
    .pin8(nQ3));  // open: pin2, pin3, pin12, pin11
  _7474 #(.ShowInternalStructure("true")) u_7474_2 (
    .pin1(In6), .pin4(n7414_2_pin2), .pin5(Q6), .pin6(nQ6), .pin13(In9), .pin10(n7414_2_pin12), .pin9(Q9),
    .pin8(nQ9));  // open: pin2, pin3, pin12, pin11
  _7474 #(.ShowInternalStructure("true")) u_7474_3 (
    .pin1(In12), .pin4(n7414_3_pin2), .pin5(Q12), .pin6(nQ12), .pin13(In14), .pin10(n7414_3_pin12),
    .pin9(Q14), .pin8(nQ14));  // open: pin2, pin3, pin12, pin11
  _7474 #(.ShowInternalStructure("true")) u_7474_4 (
    .pin1(In1), .pin4(n7414_1_pin4), .pin5(Q1), .pin6(nQ1), .pin13(In4), .pin10(n7414_1_pin10), .pin9(Q4),
    .pin8(nQ4));  // open: pin2, pin3, pin12, pin11
  _7474 #(.ShowInternalStructure("true")) u_7474_5 (
    .pin1(In7), .pin4(n7414_2_pin4), .pin5(Q7), .pin6(nQ7), .pin13(In10), .pin10(n7414_2_pin10), .pin9(Q10),
    .pin8(nQ10));  // open: pin2, pin3, pin12, pin11
  _7474 #(.ShowInternalStructure("true")) u_7474_6 (
    .pin1(In13), .pin4(n7414_3_pin4), .pin5(Q13), .pin6(nQ13), .pin13(In15), .pin10(n7414_3_pin10),
    .pin9(Q15), .pin8(nQ15));  // open: pin2, pin3, pin12, pin11
  _7474 #(.ShowInternalStructure("true")) u_7474_7 (
    .pin1(In2), .pin4(n7414_1_pin6), .pin5(Q2), .pin6(nQ2), .pin13(In5), .pin10(n7414_1_pin8), .pin9(Q5),
    .pin8(nQ5));  // open: pin2, pin3, pin12, pin11
  _7474 #(.ShowInternalStructure("true")) u_7474_8 (
    .pin1(In8), .pin4(n7414_2_pin6), .pin5(Q8), .pin6(nQ8), .pin13(In11), .pin10(n7414_2_pin8), .pin9(Q11),
    .pin8(nQ11));  // open: pin2, pin3, pin12, pin11
endmodule

module x16bitArithmeticUnit (
  input  [15:0] Ain,
  input  [15:0] Bin,
  input  Sub,
  input  Power,
  output [15:0] Result,
  output Overflow
);

  wire n7486_1_pin3, n7486_1_pin6, n7486_1_pin7, n7486_1_pin8, n7486_1_pin11, n7486_2_pin3, n7486_2_pin6,
       n7486_2_pin8, n7486_2_pin11, n7486_3_pin3, n7486_3_pin7, n7486_3_pin8, n7486_3_pin11, n7486_4_pin3,
       n7486_4_pin8, n7486_4_pin11, n74283_1_pin9, n74283_2_pin9, n74283_3_pin9;

  _7486 #(.ShowInternalStructure("true"), .VccGndPorts("true")) u_7486_1 (
    .pin1(Bin[0]), .pin2(Sub), .pin3(n7486_1_pin3), .pin4(Bin[1]), .pin5(Sub), .pin6(n7486_1_pin6),
    .pin7(n7486_1_pin7), .pin14(Power), .pin13(Bin[3]), .pin12(Sub), .pin11(n7486_1_pin11), .pin10(Bin[2]),
    .pin9(Sub), .pin8(n7486_1_pin8));
  _74283 #(.ShowInternalStructure("true"), .VccGndPorts("true")) u_74283_1 (
    .pin1(Result[1]), .pin2(n7486_1_pin6), .pin3(Ain[1]), .pin4(Result[0]), .pin5(Ain[0]),
    .pin6(n7486_1_pin3), .pin7(Sub), .pin8(n7486_1_pin7), .pin16(Power), .pin15(n7486_1_pin8),
    .pin14(Ain[2]), .pin13(Result[2]), .pin12(Ain[3]), .pin11(n7486_1_pin11), .pin10(Result[3]),
    .pin9(n74283_1_pin9));
  _7486 #(.ShowInternalStructure("true"), .VccGndPorts("true")) u_7486_2 (
    .pin1(Bin[4]), .pin2(Sub), .pin3(n7486_2_pin3), .pin4(Bin[5]), .pin5(Sub), .pin6(n7486_2_pin6),
    .pin7(n7486_1_pin7), .pin14(Power), .pin13(Bin[7]), .pin12(Sub), .pin11(n7486_2_pin11), .pin10(Bin[6]),
    .pin9(Sub), .pin8(n7486_2_pin8));
  _74283 #(.ShowInternalStructure("true"), .VccGndPorts("true")) u_74283_2 (
    .pin1(Result[5]), .pin2(n7486_2_pin6), .pin3(Ain[5]), .pin4(Result[4]), .pin5(Ain[4]),
    .pin6(n7486_2_pin3), .pin7(n74283_1_pin9), .pin8(n7486_1_pin7), .pin16(Power), .pin15(n7486_2_pin8),
    .pin14(Ain[6]), .pin13(Result[6]), .pin12(Ain[7]), .pin11(n7486_2_pin11), .pin10(Result[7]),
    .pin9(n74283_2_pin9));
  _7486 #(.ShowInternalStructure("true"), .VccGndPorts("true")) u_7486_3 (
    .pin1(Bin[8]), .pin2(Sub), .pin3(n7486_3_pin3), .pin4(Bin[9]), .pin5(Sub), .pin6(Result[9]),
    .pin7(n7486_3_pin7), .pin14(Power), .pin13(Bin[11]), .pin12(Sub), .pin11(n7486_3_pin11), .pin10(Bin[10]),
    .pin9(Sub), .pin8(n7486_3_pin8));
  _74283 #(.ShowInternalStructure("true"), .VccGndPorts("true")) u_74283_3 (
    .pin2(Result[9]), .pin3(Ain[9]), .pin4(Result[8]), .pin5(Ain[8]), .pin6(n7486_3_pin3),
    .pin7(n74283_2_pin9), .pin8(n7486_3_pin7), .pin16(Power), .pin15(n7486_3_pin8), .pin14(Ain[10]),
    .pin13(Result[10]), .pin12(Ain[11]), .pin11(n7486_3_pin11), .pin10(Result[11]), .pin9(n74283_3_pin9));  // open: pin1
  _7486 #(.ShowInternalStructure("true"), .VccGndPorts("true")) u_7486_4 (
    .pin1(Bin[12]), .pin2(Sub), .pin3(n7486_4_pin3), .pin4(Bin[13]), .pin5(Sub), .pin6(Result[13]),
    .pin7(n7486_3_pin7), .pin14(Power), .pin13(Bin[15]), .pin12(Sub), .pin11(n7486_4_pin11), .pin10(Bin[14]),
    .pin9(Sub), .pin8(n7486_4_pin8));
  _74283 #(.ShowInternalStructure("true"), .VccGndPorts("true")) u_74283_4 (
    .pin2(Result[13]), .pin3(Ain[13]), .pin4(Result[12]), .pin5(Ain[12]), .pin6(n7486_4_pin3),
    .pin7(n74283_3_pin9), .pin8(n7486_3_pin7), .pin16(Power), .pin15(n7486_4_pin8), .pin14(Ain[14]),
    .pin13(Result[14]), .pin12(Ain[15]), .pin11(n7486_4_pin11), .pin10(Result[15]), .pin9(Overflow));  // open: pin1
  // also tied to GND on the sheet: {n7486_1_pin7, n7486_3_pin7}
endmodule

module x16bitLogicUnit (
  input  [1:0] OperationSelect,
  input  [15:0] Ain,
  input  [15:0] Bin,
  input  Power,
  output [15:0] Result
);

  wire n7408_1_pin7, n7408_2_pin7, n7408_3_pin7, n7408_4_pin7, n7414_1_pin7, n7414_2_pin7, n7414_3_pin7,
       n7414_4_pin7, n7432_1_pin7, n7432_2_pin7, n7432_3_pin7, n7432_4_pin7, n7486_1_pin7, n7486_2_pin7,
       n7486_3_pin7, n7486_4_pin7, n74153_1_pin1, n74153_1_pin8, n74153_2_pin1, n74153_2_pin8, n74153_3_pin1,
       n74153_4_pin1, n74153_5_pin1, n74153_6_pin1, n74153_7_pin1, n74153_8_pin1;
  wire [7:0] n7408_1_pin11, n7408_2_pin11, n7414_1_pin12, n7414_2_pin12, n7432_1_pin11, n7432_2_pin11,
       n7486_1_pin11, n7486_2_pin11;

  _7432 #(.ShowInternalStructure("true"), .VccGndPorts("true")) u_7432_1 (
    .pin1(Ain[2]), .pin2(Bin[2]), .pin3(n7432_1_pin11[2]), .pin4(Ain[3]), .pin5(Bin[3]),
    .pin6(n7432_1_pin11[3]), .pin7(n7432_1_pin7), .pin14(Power), .pin13(Ain[0]), .pin12(Bin[0]),
    .pin11(n7432_1_pin11[0]), .pin10(Ain[1]), .pin9(Bin[1]), .pin8(n7432_1_pin11[1]));
  _7486 #(.ShowInternalStructure("true"), .VccGndPorts("true")) u_7486_1 (
    .pin1(Ain[2]), .pin2(Bin[2]), .pin3(n7486_1_pin11[2]), .pin4(Ain[3]), .pin5(Bin[3]),
    .pin6(n7486_1_pin11[3]), .pin7(n7486_1_pin7), .pin14(Power), .pin13(Ain[0]), .pin12(Bin[0]),
    .pin11(n7486_1_pin11[0]), .pin10(Ain[1]), .pin9(Bin[1]), .pin8(n7486_1_pin11[1]));
  _7432 #(.ShowInternalStructure("true"), .VccGndPorts("true")) u_7432_2 (
    .pin1(Ain[10]), .pin2(Bin[10]), .pin3(n7432_2_pin11[2]), .pin4(Ain[11]), .pin5(Bin[11]),
    .pin6(n7432_2_pin11[3]), .pin7(n7432_2_pin7), .pin14(Power), .pin13(Ain[8]), .pin12(Bin[8]),
    .pin11(n7432_2_pin11[0]), .pin10(Ain[9]), .pin9(Bin[9]), .pin8(n7432_2_pin11[1]));
  _7486 #(.ShowInternalStructure("true"), .VccGndPorts("true")) u_7486_2 (
    .pin1(Ain[10]), .pin2(Bin[10]), .pin3(n7486_2_pin11[2]), .pin4(Ain[11]), .pin5(Bin[11]),
    .pin6(n7486_2_pin11[3]), .pin7(n7486_2_pin7), .pin14(Power), .pin13(Ain[8]), .pin12(Bin[8]),
    .pin11(n7486_2_pin11[0]), .pin10(Ain[9]), .pin9(Bin[9]), .pin8(n7486_2_pin11[1]));
  _7432 #(.ShowInternalStructure("true"), .VccGndPorts("true")) u_7432_3 (
    .pin1(Ain[6]), .pin2(Bin[6]), .pin3(n7432_1_pin11[6]), .pin4(Ain[7]), .pin5(Bin[7]),
    .pin6(n7432_1_pin11[7]), .pin7(n7432_3_pin7), .pin14(Power), .pin13(Ain[4]), .pin12(Bin[4]),
    .pin11(n7432_1_pin11[4]), .pin10(Ain[5]), .pin9(Bin[5]), .pin8(n7432_1_pin11[5]));
  _7486 #(.ShowInternalStructure("true"), .VccGndPorts("true")) u_7486_3 (
    .pin1(Ain[6]), .pin2(Bin[6]), .pin3(n7486_1_pin11[6]), .pin4(Ain[7]), .pin5(Bin[7]),
    .pin6(n7486_1_pin11[7]), .pin7(n7486_3_pin7), .pin14(Power), .pin13(Ain[4]), .pin12(Bin[4]),
    .pin11(n7486_1_pin11[4]), .pin10(Ain[5]), .pin9(Bin[5]), .pin8(n7486_1_pin11[5]));
  _7432 #(.ShowInternalStructure("true"), .VccGndPorts("true")) u_7432_4 (
    .pin1(Ain[14]), .pin2(Bin[14]), .pin3(n7432_2_pin11[6]), .pin4(Ain[15]), .pin5(Bin[15]),
    .pin6(n7432_2_pin11[7]), .pin7(n7432_4_pin7), .pin14(Power), .pin13(Ain[12]), .pin12(Bin[12]),
    .pin11(n7432_2_pin11[4]), .pin10(Ain[13]), .pin9(Bin[13]), .pin8(n7432_2_pin11[5]));
  _7486 #(.ShowInternalStructure("true"), .VccGndPorts("true")) u_7486_4 (
    .pin1(Ain[14]), .pin2(Bin[14]), .pin3(n7486_2_pin11[6]), .pin4(Ain[15]), .pin5(Bin[15]),
    .pin6(n7486_2_pin11[7]), .pin7(n7486_4_pin7), .pin14(Power), .pin13(Ain[12]), .pin12(Bin[12]),
    .pin11(n7486_2_pin11[4]), .pin10(Ain[13]), .pin9(Bin[13]), .pin8(n7486_2_pin11[5]));
  _7408 #(.ShowInternalStructure("true"), .VccGndPorts("true")) u_7408_1 (
    .pin1(Ain[2]), .pin2(Bin[2]), .pin3(n7408_1_pin11[2]), .pin4(Ain[3]), .pin5(Bin[3]),
    .pin6(n7408_1_pin11[3]), .pin7(n7408_1_pin7), .pin14(Power), .pin13(Ain[0]), .pin12(Bin[0]),
    .pin11(n7408_1_pin11[0]), .pin10(Ain[1]), .pin9(Bin[1]), .pin8(n7408_1_pin11[1]));
  _7414 #(.ShowInternalStructure("true"), .VccGndPorts("true")) u_7414_1 (
    .pin1(Ain[2]), .pin2(n7414_1_pin12[2]), .pin3(Ain[3]), .pin4(n7414_1_pin12[3]), .pin7(n7414_1_pin7),
    .pin14(Power), .pin13(Ain[0]), .pin12(n7414_1_pin12[0]), .pin11(Ain[1]), .pin10(n7414_1_pin12[1]));  // open: pin5, pin6, pin9, pin8
  _7408 #(.ShowInternalStructure("true"), .VccGndPorts("true")) u_7408_2 (
    .pin1(Ain[10]), .pin2(Bin[10]), .pin3(n7408_2_pin11[2]), .pin4(Ain[11]), .pin5(Bin[11]),
    .pin6(n7408_2_pin11[3]), .pin7(n7408_2_pin7), .pin14(Power), .pin13(Ain[8]), .pin12(Bin[8]),
    .pin11(n7408_2_pin11[0]), .pin10(Ain[9]), .pin9(Bin[9]), .pin8(n7408_2_pin11[1]));
  _7414 #(.ShowInternalStructure("true"), .VccGndPorts("true")) u_7414_2 (
    .pin1(Ain[10]), .pin2(n7414_2_pin12[2]), .pin3(Ain[11]), .pin4(n7414_2_pin12[3]), .pin7(n7414_2_pin7),
    .pin14(Power), .pin13(Ain[8]), .pin12(n7414_2_pin12[0]), .pin11(Ain[9]), .pin10(n7414_2_pin12[1]));  // open: pin5, pin6, pin9, pin8
  _7408 #(.ShowInternalStructure("true"), .VccGndPorts("true")) u_7408_3 (
    .pin1(Ain[6]), .pin2(Bin[6]), .pin3(n7408_1_pin11[6]), .pin4(Ain[7]), .pin5(Bin[7]),
    .pin6(n7408_1_pin11[7]), .pin7(n7408_3_pin7), .pin14(Power), .pin13(Ain[4]), .pin12(Bin[4]),
    .pin11(n7408_1_pin11[4]), .pin10(Ain[5]), .pin9(Bin[5]), .pin8(n7408_1_pin11[5]));
  _7414 #(.ShowInternalStructure("true"), .VccGndPorts("true")) u_7414_3 (
    .pin1(Ain[6]), .pin2(n7414_1_pin12[6]), .pin3(Ain[7]), .pin4(n7414_1_pin12[7]), .pin7(n7414_3_pin7),
    .pin14(Power), .pin13(Ain[4]), .pin12(n7414_1_pin12[4]), .pin11(Ain[5]), .pin10(n7414_1_pin12[5]));  // open: pin5, pin6, pin9, pin8
  _7408 #(.ShowInternalStructure("true"), .VccGndPorts("true")) u_7408_4 (
    .pin1(Ain[14]), .pin2(Bin[14]), .pin3(n7408_2_pin11[6]), .pin4(Ain[15]), .pin5(Bin[15]),
    .pin6(n7408_2_pin11[7]), .pin7(n7408_4_pin7), .pin14(Power), .pin13(Ain[12]), .pin12(Bin[12]),
    .pin11(n7408_2_pin11[4]), .pin10(Ain[13]), .pin9(Bin[13]), .pin8(n7408_2_pin11[5]));
  _7414 #(.ShowInternalStructure("true"), .VccGndPorts("true")) u_7414_4 (
    .pin1(Ain[14]), .pin2(n7414_2_pin12[6]), .pin3(Ain[15]), .pin4(n7414_2_pin12[7]), .pin7(n7414_4_pin7),
    .pin14(Power), .pin13(Ain[12]), .pin12(n7414_2_pin12[4]), .pin11(Ain[13]), .pin10(n7414_2_pin12[5]));  // open: pin5, pin6, pin9, pin8
  _74153 #(.ShowInternalStructure("true"), .VccGndPorts("true")) u_74153_1 (
    .pin1(n74153_1_pin1), .pin2(OperationSelect[1]), .pin3(n7414_1_pin12[7]), .pin4(n7486_1_pin11[7]),
    .pin5(n7408_1_pin11[7]), .pin6(n7432_1_pin11[7]), .pin7(Result[7]), .pin8(n74153_1_pin8), .pin16(Power),
    .pin15(n74153_1_pin1), .pin14(OperationSelect[0]), .pin13(n7414_1_pin12[6]), .pin12(n7486_1_pin11[6]),
    .pin11(n7408_1_pin11[6]), .pin10(n7432_1_pin11[6]), .pin9(Result[6]));
  _74153 #(.ShowInternalStructure("true"), .VccGndPorts("true")) u_74153_2 (
    .pin1(n74153_2_pin1), .pin2(OperationSelect[1]), .pin3(n7414_2_pin12[7]), .pin4(n7486_2_pin11[7]),
    .pin5(n7408_2_pin11[7]), .pin6(n7432_2_pin11[7]), .pin7(Result[15]), .pin8(n74153_2_pin8), .pin16(Power),
    .pin15(n74153_2_pin1), .pin14(OperationSelect[0]), .pin13(n7414_2_pin12[6]), .pin12(n7486_2_pin11[6]),
    .pin11(n7408_2_pin11[6]), .pin10(n7432_2_pin11[6]), .pin9(Result[14]));
  _74153 #(.ShowInternalStructure("true"), .VccGndPorts("true")) u_74153_3 (
    .pin1(n74153_3_pin1), .pin2(OperationSelect[1]), .pin3(n7414_1_pin12[5]), .pin4(n7486_1_pin11[5]),
    .pin5(n7408_1_pin11[5]), .pin6(n7432_1_pin11[5]), .pin7(Result[5]), .pin8(n74153_1_pin8), .pin16(Power),
    .pin15(n74153_3_pin1), .pin14(OperationSelect[0]), .pin13(n7414_1_pin12[4]), .pin12(n7486_1_pin11[4]),
    .pin11(n7408_1_pin11[4]), .pin10(n7432_1_pin11[4]), .pin9(Result[4]));
  _74153 #(.ShowInternalStructure("true"), .VccGndPorts("true")) u_74153_4 (
    .pin1(n74153_4_pin1), .pin2(OperationSelect[1]), .pin3(n7414_2_pin12[5]), .pin4(n7486_2_pin11[5]),
    .pin5(n7408_2_pin11[5]), .pin6(n7432_2_pin11[5]), .pin7(Result[13]), .pin8(n74153_2_pin8), .pin16(Power),
    .pin15(n74153_4_pin1), .pin14(OperationSelect[0]), .pin13(n7414_2_pin12[4]), .pin12(n7486_2_pin11[4]),
    .pin11(n7408_2_pin11[4]), .pin10(n7432_2_pin11[4]), .pin9(Result[12]));
  _74153 #(.ShowInternalStructure("true"), .VccGndPorts("true")) u_74153_5 (
    .pin1(n74153_5_pin1), .pin2(OperationSelect[1]), .pin3(n7414_1_pin12[3]), .pin4(n7486_1_pin11[3]),
    .pin5(n7408_1_pin11[3]), .pin6(n7432_1_pin11[3]), .pin7(Result[3]), .pin8(n74153_1_pin8), .pin16(Power),
    .pin15(n74153_5_pin1), .pin14(OperationSelect[0]), .pin13(n7414_1_pin12[2]), .pin12(n7486_1_pin11[2]),
    .pin11(n7408_1_pin11[2]), .pin10(n7432_1_pin11[2]), .pin9(Result[2]));
  _74153 #(.ShowInternalStructure("true"), .VccGndPorts("true")) u_74153_6 (
    .pin1(n74153_6_pin1), .pin2(OperationSelect[1]), .pin3(n7414_2_pin12[3]), .pin4(n7486_2_pin11[3]),
    .pin5(n7408_2_pin11[3]), .pin6(n7432_2_pin11[3]), .pin7(Result[11]), .pin8(n74153_2_pin8), .pin16(Power),
    .pin15(n74153_6_pin1), .pin14(OperationSelect[0]), .pin13(n7414_2_pin12[2]), .pin12(n7486_2_pin11[2]),
    .pin11(n7408_2_pin11[2]), .pin10(n7432_2_pin11[2]), .pin9(Result[10]));
  _74153 #(.ShowInternalStructure("true"), .VccGndPorts("true")) u_74153_7 (
    .pin1(n74153_7_pin1), .pin2(OperationSelect[1]), .pin3(n7414_1_pin12[1]), .pin4(n7486_1_pin11[1]),
    .pin5(n7408_1_pin11[1]), .pin6(n7432_1_pin11[1]), .pin7(Result[1]), .pin8(n74153_1_pin8), .pin16(Power),
    .pin15(n74153_7_pin1), .pin14(OperationSelect[0]), .pin13(n7414_1_pin12[0]), .pin12(n7486_1_pin11[0]),
    .pin11(n7408_1_pin11[0]), .pin10(n7432_1_pin11[0]), .pin9(Result[0]));
  _74153 #(.ShowInternalStructure("true"), .VccGndPorts("true")) u_74153_8 (
    .pin1(n74153_8_pin1), .pin2(OperationSelect[1]), .pin3(n7414_2_pin12[1]), .pin4(n7486_2_pin11[1]),
    .pin5(n7408_2_pin11[1]), .pin6(n7432_2_pin11[1]), .pin7(Result[9]), .pin8(n74153_2_pin8), .pin16(Power),
    .pin15(n74153_8_pin1), .pin14(OperationSelect[0]), .pin13(n7414_2_pin12[0]), .pin12(n7486_2_pin11[0]),
    .pin11(n7408_2_pin11[0]), .pin10(n7432_2_pin11[0]), .pin9(Result[8]));
  // also tied to GND on the sheet: {n7432_1_pin7, n7486_1_pin7, n7432_2_pin7, n7486_2_pin7, n7432_3_pin7, n7486_3_pin7, n7432_4_pin7, n7486_4_pin7, n7408_1_pin7, n7414_1_pin7, n7408_2_pin7, n7414_2_pin7, n7408_3_pin7, n7414_3_pin7, n7408_4_pin7, n7414_4_pin7, n74153_1_pin1, n74153_2_pin1, n74153_3_pin1, n74153_4_pin1, n74153_5_pin1, n74153_6_pin1, n74153_7_pin1, n74153_8_pin1, n74153_1_pin8, n74153_2_pin8}
endmodule

module ALU (
  input  AllowIn,
  input  AllowOut,
  input  AccumulatorClock,
  input  [4:0] IR4t0,
  input  [15:0] DataBusIn,
  input  EndInst,
  input  nClearAccumulator,
  output [15:0] AccumulatorBus,
  output [15:0] AccumulatorOut,
  output Zero,
  output Negative,
  output Overflow,
  output Underflow,
  output AlessB,
  output AisB,
  output AgreatB
);

  wire n7400_1_pin8, n7400_1_pin11, n7400_2_pin1, n7400_2_pin3, n7400_2_pin6, n7400_2_pin11, n7414_1_pin2,
       n7414_1_pin4, n7414_1_pin6, n7414_1_pin8, n7414_1_pin10, n7414_2_pin2, n7414_2_pin4, n7414_2_pin6,
       n7432_1_pin3, n7432_1_pin6, n7432_1_pin8, n7432_1_pin11, n7432_2_pin11, n7442_1_pin1, n7442_1_pin2,
       n7442_1_pin3, n7442_1_pin4, n7442_1_pin5, n7442_1_pin6, n7442_1_pin7, n7442_1_pin9, n74541_1_pin1,
       not_1_out, not_2_out, not_3_out, pull_resistor_1_node, shifthandler_1_nof, shifthandler_1_nuf,
       transistor_2_out, transistor_3_out, x16bitarithmeticunit_1_overflow;
  wire [15:0] n74541_2_pin11;

  _74541 #(.ShowInternalStructure("true")) u_74541_1 (
    .pin1(n74541_1_pin1), .pin2(DataBusIn[15]), .pin3(DataBusIn[14]), .pin4(DataBusIn[13]),
    .pin5(DataBusIn[12]), .pin6(DataBusIn[11]), .pin7(DataBusIn[10]), .pin8(DataBusIn[9]),
    .pin9(DataBusIn[8]), .pin19(n74541_1_pin1), .pin18(n74541_2_pin11[15]), .pin17(n74541_2_pin11[14]),
    .pin16(n74541_2_pin11[13]), .pin15(n74541_2_pin11[12]), .pin14(n74541_2_pin11[11]),
    .pin13(n74541_2_pin11[10]), .pin12(n74541_2_pin11[9]), .pin11(n74541_2_pin11[8]));
  _7400 #(.ShowInternalStructure("true")) u_7400_1 (
    .pin13(IR4t0[4]), .pin12(IR4t0[4]), .pin11(n7400_1_pin11), .pin10(n7400_1_pin11), .pin9(IR4t0[3]),
    .pin8(n7400_1_pin8));  // open: pin1, pin2, pin3, pin4, pin5, pin6
  _74541 #(.ShowInternalStructure("true")) u_74541_2 (
    .pin1(n74541_1_pin1), .pin2(DataBusIn[7]), .pin3(DataBusIn[6]), .pin4(DataBusIn[5]), .pin5(DataBusIn[4]),
    .pin6(DataBusIn[3]), .pin7(DataBusIn[2]), .pin8(DataBusIn[1]), .pin9(DataBusIn[0]),
    .pin19(n74541_1_pin1), .pin18(n74541_2_pin11[7]), .pin17(n74541_2_pin11[6]), .pin16(n74541_2_pin11[5]),
    .pin15(n74541_2_pin11[4]), .pin14(n74541_2_pin11[3]), .pin13(n74541_2_pin11[2]),
    .pin12(n74541_2_pin11[1]), .pin11(n74541_2_pin11[0]));
  _7442 #(.ShowInternalStructure("true")) u_7442_1 (
    .pin1(n7442_1_pin1), .pin2(n7442_1_pin2), .pin3(n7442_1_pin3), .pin4(n7442_1_pin4), .pin5(n7442_1_pin5),
    .pin6(n7442_1_pin6), .pin7(n7442_1_pin7), .pin15(IR4t0[0]), .pin14(IR4t0[1]), .pin13(IR4t0[2]),
    .pin12(n7400_1_pin8), .pin9(n7442_1_pin9));  // open: pin11, pin10
  _7414 #(.ShowInternalStructure("true")) u_7414_1 (
    .pin1(n7442_1_pin1), .pin2(n7414_1_pin2), .pin3(n7442_1_pin2), .pin4(n7414_1_pin4), .pin5(n7442_1_pin3),
    .pin6(n7414_1_pin6), .pin13(AllowIn), .pin12(n74541_1_pin1), .pin11(n7442_1_pin7), .pin10(n7414_1_pin10),
    .pin9(n7442_1_pin9), .pin8(n7414_1_pin8));
  _7414 #(.ShowInternalStructure("true")) u_7414_2 (
    .pin1(n7442_1_pin4), .pin2(n7414_2_pin2), .pin3(n7442_1_pin5), .pin4(n7414_2_pin4), .pin5(n7442_1_pin6),
    .pin6(n7414_2_pin6));  // open: pin13, pin12, pin11, pin10, pin9, pin8
  _7432 #(.ShowInternalStructure("true")) u_7432_1 (
    .pin1(n7414_1_pin2), .pin2(n7414_1_pin4), .pin3(n7432_1_pin3), .pin4(n7414_1_pin6), .pin5(n7414_2_pin2),
    .pin6(n7432_1_pin6), .pin13(n7414_2_pin4), .pin12(n7414_2_pin6), .pin11(n7432_1_pin11),
    .pin10(n7432_1_pin11), .pin9(n7414_1_pin8), .pin8(n7432_1_pin8));
  Accumulator accumulator_1 (
    .DataIn(n74541_2_pin11), .Clock(AccumulatorClock), .nClear(nClearAccumulator), .DataOut(AccumulatorOut),
    .Zero(Zero), .Neg(Negative));
  _7432 #(.ShowInternalStructure("true")) u_7432_2 (
    .pin13(n7432_1_pin8), .pin12(n7414_1_pin10), .pin11(n7432_2_pin11));  // open: pin1, pin2, pin3, pin4, pin5, pin6, pin10, pin9, pin8
  _74541 #(.ShowInternalStructure("true")) u_74541_3 (
    .pin1(AllowOut), .pin2(AccumulatorOut[15]), .pin3(AccumulatorOut[14]), .pin4(AccumulatorOut[13]),
    .pin5(AccumulatorOut[12]), .pin6(AccumulatorOut[11]), .pin7(AccumulatorOut[10]),
    .pin8(AccumulatorOut[9]), .pin9(AccumulatorOut[8]), .pin19(AllowOut), .pin18(AccumulatorBus[15]),
    .pin17(AccumulatorBus[14]), .pin16(AccumulatorBus[13]), .pin15(AccumulatorBus[12]),
    .pin14(AccumulatorBus[11]), .pin13(AccumulatorBus[10]), .pin12(AccumulatorBus[9]),
    .pin11(AccumulatorBus[8]));
  not not_1 (not_1_out, n7432_1_pin3);
  Pull_Resistor pull_resistor_1 (.node(pull_resistor_1_node));
  Transistor transistor_1 (.in(1'b1), .out(pull_resistor_1_node), .gate(not_1_out));
  not not_2 (not_2_out, n7432_1_pin6);
  Transistor transistor_2 (.in(1'b1), .out(transistor_2_out), .gate(not_2_out));
  not not_3 (not_3_out, n7432_2_pin11);
  Transistor transistor_3 (.in(1'b1), .out(transistor_3_out), .gate(not_3_out));
  Pull_Resistor pull_resistor_2 (.node(transistor_3_out));
  Pull_Resistor pull_resistor_3 (.node(transistor_2_out));
  _74541 #(.ShowInternalStructure("true")) u_74541_4 (
    .pin1(AllowOut), .pin2(AccumulatorOut[7]), .pin3(AccumulatorOut[6]), .pin4(AccumulatorOut[5]),
    .pin5(AccumulatorOut[4]), .pin6(AccumulatorOut[3]), .pin7(AccumulatorOut[2]), .pin8(AccumulatorOut[1]),
    .pin9(AccumulatorOut[0]), .pin19(AllowOut), .pin18(AccumulatorBus[7]), .pin17(AccumulatorBus[6]),
    .pin16(AccumulatorBus[5]), .pin15(AccumulatorBus[4]), .pin14(AccumulatorBus[3]),
    .pin13(AccumulatorBus[2]), .pin12(AccumulatorBus[1]), .pin11(AccumulatorBus[0]));
  x16bitArithmeticUnit x16bitarithmeticunit_1 (
    .Ain(AccumulatorOut), .Bin(DataBusIn), .Sub(n7442_1_pin1), .Power(pull_resistor_1_node),
    .Result(n74541_2_pin11), .Overflow(x16bitarithmeticunit_1_overflow));
  ShiftHandler shifthandler_1 (
    .RLF(n7442_1_pin3), .Ain(AccumulatorOut), .Power(transistor_2_out), .nUF(shifthandler_1_nuf),
    .nOF(shifthandler_1_nof), .ShiftOut(n74541_2_pin11));
  x16bitLogicUnit x16bitlogicunit_1 (
    .OperationSelect({IR4t0[1], IR4t0[2]}), .Ain(AccumulatorOut), .Bin(DataBusIn), .Power(transistor_3_out),
    .Result(n74541_2_pin11));
  Pull_Resistor pull_resistor_4 (.node(AisB));
  Pull_Resistor pull_resistor_5 (.node(AlessB));
  Pull_Resistor pull_resistor_6 (.node(AgreatB));
  x16bitComparitor x16bitcomparitor_1 (
    .Ain(AccumulatorOut), .Bin(DataBusIn), .Power(1'b1), .AisB(AisB), .AlessB(AlessB), .AgreaterB(AgreatB));
  Pull_Resistor pull_resistor_7 (.node(x16bitarithmeticunit_1_overflow));
  Pull_Resistor #(.pull(1)) pull_resistor_8 (.node(shifthandler_1_nuf));
  Pull_Resistor #(.pull(1)) pull_resistor_9 (.node(shifthandler_1_nof));
  _7400 #(.ShowInternalStructure("true")) u_7400_2 (
    .pin1(n7400_2_pin1), .pin2(n7400_2_pin1), .pin3(n7400_2_pin3), .pin4(EndInst), .pin5(EndInst),
    .pin6(n7400_2_pin6), .pin13(x16bitarithmeticunit_1_overflow), .pin12(x16bitarithmeticunit_1_overflow),
    .pin11(n7400_2_pin11), .pin10(n7400_2_pin11), .pin9(shifthandler_1_nof), .pin8(n7400_2_pin1));
  _7474 #(.ShowInternalStructure("true")) u_7474_1 (
    .pin1(n7400_2_pin6), .pin4(n7400_2_pin3), .pin5(Overflow), .pin13(n7400_2_pin6),
    .pin10(shifthandler_1_nuf), .pin9(Underflow));  // open: pin2, pin3, pin6, pin12, pin11, pin8
endmodule

module ProgramCounter (
  input  [15:0] DataBusIn,
  input  CallJump,
  input  stackReturn,
  input  CLR,
  input  Clk,
  input  Skip,
  output S0,
  output S1,
  output [15:0] PCout,
  output EndInst
);

  wire n7400_1_pin3, n7400_1_pin6, n7400_1_pin8, n7400_1_pin11, n7408_1_pin3, n7408_1_pin8, n7408_1_pin11,
       n7408_2_pin3, n7414_1_pin1, n7414_1_pin2, n7414_1_pin4, n7414_1_pin6, n7414_1_pin8, n7414_1_pin9,
       n7414_1_pin10, n7414_2_pin2, n7414_2_pin4, n7414_2_pin6, n7414_2_pin9, n7414_3_pin1, n7414_3_pin2,
       n7414_3_pin4, n7414_3_pin6, n7414_3_pin8, n7414_3_pin10, n7432_1_pin1, n7432_2_pin1, n7432_2_pin11,
       n7474_1_pin10, n7474_1_pin12, n74193_1_pin4, n74193_1_pin12, n74193_1_pin13, n74193_2_pin12,
       n74193_2_pin13, n74193_3_pin12, n74193_3_pin13;

  _7414 #(.ShowInternalStructure("true")) u_7414_1 (
    .pin1(n7414_1_pin1), .pin2(n7414_1_pin2), .pin3(n7414_1_pin2), .pin4(n7414_1_pin4), .pin5(n7414_1_pin4),
    .pin6(n7414_1_pin6), .pin13(stackReturn), .pin12(n7414_1_pin1), .pin11(CallJump), .pin10(n7414_1_pin10),
    .pin9(n7414_1_pin9), .pin8(n7414_1_pin8));
  _7400 #(.ShowInternalStructure("true")) u_7400_1 (
    .pin1(n7414_1_pin6), .pin2(n7414_1_pin1), .pin3(n7400_1_pin3), .pin4(n7400_1_pin3), .pin5(n7400_1_pin3),
    .pin6(n7400_1_pin6), .pin13(n7414_1_pin10), .pin12(n7414_1_pin1), .pin11(n7400_1_pin11),
    .pin10(n7400_1_pin11), .pin9(n7400_1_pin11), .pin8(n7400_1_pin8));
  _7474 #(.ShowInternalStructure("true")) u_7474_1 (
    .pin13(n7414_1_pin8), .pin12(n7474_1_pin12), .pin11(EndInst), .pin10(n7474_1_pin10), .pin9(S1), .pin8(S0));  // open: pin1, pin2, pin3, pin4, pin5, pin6
  _7432 #(.ShowInternalStructure("true")) u_7432_1 (
    .pin1(n7432_1_pin1), .pin2(CLR), .pin3(n7414_1_pin9));  // open: pin4, pin5, pin6, pin13, pin12, pin11, pin10, pin9, pin8
  _7414 #(.ShowInternalStructure("true")) u_7414_2 (
    .pin1(Clk), .pin2(n7414_2_pin2), .pin3(n7414_2_pin2), .pin4(n7414_2_pin4), .pin5(n7414_2_pin4),
    .pin6(n7414_2_pin6), .pin9(n7414_2_pin9), .pin8(n7474_1_pin10));  // open: pin13, pin12, pin11, pin10
  _7414 #(.ShowInternalStructure("true")) u_7414_3 (
    .pin1(n7414_3_pin1), .pin2(n7414_3_pin2), .pin3(n7414_3_pin2), .pin4(n7414_3_pin4), .pin5(n7414_3_pin4),
    .pin6(n7414_3_pin6), .pin13(Skip), .pin12(n7414_3_pin1), .pin11(n7414_3_pin1), .pin10(n7414_3_pin10),
    .pin9(n7414_3_pin10), .pin8(n7414_3_pin8));
  _7408 #(.ShowInternalStructure("true")) u_7408_1 (
    .pin1(n7414_2_pin6), .pin2(Clk), .pin3(n7408_1_pin3), .pin4(n7408_1_pin3), .pin5(S0),
    .pin6(n7414_2_pin9), .pin13(n7408_1_pin3), .pin12(S1), .pin11(n7408_1_pin11), .pin10(n7408_1_pin11),
    .pin9(n7414_3_pin1), .pin8(n7408_1_pin8));
  _7408 #(.ShowInternalStructure("true")) u_7408_2 (
    .pin1(n7414_3_pin6), .pin2(n7414_3_pin1), .pin3(n7408_2_pin3), .pin13(n7414_3_pin8), .pin12(Skip),
    .pin11(n7432_1_pin1));  // open: pin4, pin5, pin6, pin10, pin9, pin8
  _7432 #(.ShowInternalStructure("true")) u_7432_2 (
    .pin1(n7432_2_pin1), .pin2(n7400_1_pin6), .pin3(EndInst), .pin13(n7408_1_pin8), .pin12(n7408_2_pin3),
    .pin11(n7432_2_pin11), .pin10(n7432_2_pin11), .pin9(n7432_1_pin1), .pin8(n7432_2_pin1));  // open: pin4, pin5, pin6
  _74193 #(.ShowInternalStructure("true")) u_74193_1 (
    .pin1(DataBusIn[1]), .pin2(PCout[1]), .pin3(PCout[0]), .pin4(n74193_1_pin4), .pin5(EndInst),
    .pin6(PCout[2]), .pin7(PCout[3]), .pin15(DataBusIn[0]), .pin14(CLR), .pin13(n74193_1_pin13),
    .pin12(n74193_1_pin12), .pin11(n7400_1_pin8), .pin10(DataBusIn[2]), .pin9(DataBusIn[3]));
  _74193 #(.ShowInternalStructure("true")) u_74193_2 (
    .pin1(DataBusIn[5]), .pin2(PCout[5]), .pin3(PCout[4]), .pin4(n74193_1_pin13), .pin5(n74193_1_pin12),
    .pin6(PCout[6]), .pin7(PCout[7]), .pin15(DataBusIn[4]), .pin14(CLR), .pin13(n74193_2_pin13),
    .pin12(n74193_2_pin12), .pin11(n7400_1_pin8), .pin10(DataBusIn[6]), .pin9(DataBusIn[7]));
  _74193 #(.ShowInternalStructure("true")) u_74193_3 (
    .pin1(DataBusIn[9]), .pin2(PCout[9]), .pin3(PCout[8]), .pin4(n74193_2_pin13), .pin5(n74193_2_pin12),
    .pin6(PCout[10]), .pin7(PCout[11]), .pin15(DataBusIn[8]), .pin14(CLR), .pin13(n74193_3_pin13),
    .pin12(n74193_3_pin12), .pin11(n7400_1_pin8), .pin10(DataBusIn[10]), .pin9(DataBusIn[11]));
  _74193 #(.ShowInternalStructure("true")) u_74193_4 (
    .pin1(DataBusIn[13]), .pin2(PCout[13]), .pin3(PCout[12]), .pin4(n74193_3_pin13), .pin5(n74193_3_pin12),
    .pin6(PCout[14]), .pin7(PCout[15]), .pin15(DataBusIn[12]), .pin14(CLR), .pin11(n7400_1_pin8),
    .pin10(DataBusIn[14]), .pin9(DataBusIn[15]));  // open: pin13, pin12
  // also tied to GND on the sheet: n7474_1_pin12
  // also tied to VCC on the sheet: n74193_1_pin4
endmodule

module Stack (
  input  Push,
  input  Pop,
  input  [15:0] PCin,
  output nSetError,
  output [15:0] StackOut
);

  wire n7408_1_pin3, n7408_1_pin6, n7408_1_pin9, n7408_1_pin10, n7414_1_pin2, n7414_1_pin12, n7432_1_pin3,
       n7432_1_pin6, n7474_1_pin5, n7474_1_pin6, n74193_1_pin11, n74193_1_pin12, n74193_1_pin13,
       n74193_1_pin14, not_1_out, not_2_out, not_3_out, not_4_out;
  wire [3:0] n74193_1_pin3, n74193_2_pin3;
  wire [7:0] ram_1_data, ram_2_data;

  _7414 #(.ShowInternalStructure("true")) u_7414_1 (
    .pin1(Pop), .pin2(n7414_1_pin2), .pin13(Push), .pin12(n7414_1_pin12));  // open: pin3, pin4, pin5, pin6, pin11, pin10, pin9, pin8
  _7474 #(.ShowInternalStructure("true")) u_7474_1 (
    .pin1(n7414_1_pin2), .pin4(n7414_1_pin12), .pin5(n7474_1_pin5), .pin6(n7474_1_pin6));  // open: pin2, pin3, pin13, pin12, pin11, pin10, pin9, pin8
  _7408 #(.ShowInternalStructure("true")) u_7408_1 (
    .pin1(n7474_1_pin5), .pin2(n7414_1_pin12), .pin3(n7408_1_pin3), .pin4(n7414_1_pin2), .pin5(n7474_1_pin6),
    .pin6(n7408_1_pin6), .pin10(n7408_1_pin10), .pin9(n7408_1_pin9), .pin8(nSetError));  // open: pin13, pin12, pin11
  _7432 #(.ShowInternalStructure("true")) u_7432_1 (
    .pin1(n7408_1_pin6), .pin2(n7474_1_pin5), .pin3(n7432_1_pin3), .pin4(n7408_1_pin3), .pin5(n7474_1_pin6),
    .pin6(n7432_1_pin6));  // open: pin13, pin12, pin11, pin10, pin9, pin8
  _74193 #(.ShowInternalStructure("true")) u_74193_1 (
    .pin2(n74193_1_pin3[1]), .pin3(n74193_1_pin3[0]), .pin4(n7432_1_pin3), .pin5(n7432_1_pin6),
    .pin6(n74193_1_pin3[2]), .pin7(n74193_1_pin3[3]), .pin14(n74193_1_pin14), .pin13(n74193_1_pin13),
    .pin12(n74193_1_pin12), .pin11(n74193_1_pin11));  // open: pin1, pin15, pin10, pin9
  _74193 #(.ShowInternalStructure("true")) u_74193_2 (
    .pin2(n74193_2_pin3[1]), .pin3(n74193_2_pin3[0]), .pin4(n74193_1_pin13), .pin5(n74193_1_pin12),
    .pin6(n74193_2_pin3[2]), .pin7(n74193_2_pin3[3]), .pin13(n7408_1_pin10), .pin12(n7408_1_pin9));  // open: pin1, pin15, pin14, pin11, pin10, pin9
  RAM #(.databus("bidir"), .trigger("high")) ram_1 (
    .addr({n74193_2_pin3, n74193_1_pin3}), .we(not_1_out), .oe(not_2_out), .data(ram_1_data));
  not not_1 (not_1_out, n7414_1_pin12);
  not not_2 (not_2_out, n7474_1_pin5);
  RAM #(.databus("bidir"), .trigger("high")) ram_2 (
    .addr({n74193_2_pin3, n74193_1_pin3}), .we(not_3_out), .oe(not_4_out), .data(ram_2_data));
  not not_3 (not_3_out, n7414_1_pin12);
  not not_4 (not_4_out, n7474_1_pin5);
  _74541 #(.ShowInternalStructure("true")) u_74541_1 (
    .pin1(n7414_1_pin12), .pin2(PCin[7]), .pin3(PCin[6]), .pin4(PCin[5]), .pin5(PCin[4]), .pin6(PCin[3]),
    .pin7(PCin[2]), .pin8(PCin[1]), .pin9(PCin[0]), .pin19(n7414_1_pin12), .pin18(ram_1_data[7]),
    .pin17(ram_1_data[6]), .pin16(ram_1_data[5]), .pin15(ram_1_data[4]), .pin14(ram_1_data[3]),
    .pin13(ram_1_data[2]), .pin12(ram_1_data[1]), .pin11(ram_1_data[0]));
  _74541 #(.ShowInternalStructure("true")) u_74541_2 (
    .pin1(n7474_1_pin5), .pin2(ram_1_data[7]), .pin3(ram_1_data[6]), .pin4(ram_1_data[5]),
    .pin5(ram_1_data[4]), .pin6(ram_1_data[3]), .pin7(ram_1_data[2]), .pin8(ram_1_data[1]),
    .pin9(ram_1_data[0]), .pin19(n7474_1_pin5), .pin18(StackOut[7]), .pin17(StackOut[6]),
    .pin16(StackOut[5]), .pin15(StackOut[4]), .pin14(StackOut[3]), .pin13(StackOut[2]), .pin12(StackOut[1]),
    .pin11(StackOut[0]));
  _74541 #(.ShowInternalStructure("true")) u_74541_3 (
    .pin1(n7414_1_pin12), .pin2(PCin[15]), .pin3(PCin[14]), .pin4(PCin[13]), .pin5(PCin[12]),
    .pin6(PCin[11]), .pin7(PCin[10]), .pin8(PCin[9]), .pin9(PCin[8]), .pin19(n7414_1_pin12),
    .pin18(ram_2_data[7]), .pin17(ram_2_data[6]), .pin16(ram_2_data[5]), .pin15(ram_2_data[4]),
    .pin14(ram_2_data[3]), .pin13(ram_2_data[2]), .pin12(ram_2_data[1]), .pin11(ram_2_data[0]));
  _74541 #(.ShowInternalStructure("true")) u_74541_4 (
    .pin1(n7474_1_pin5), .pin2(ram_2_data[7]), .pin3(ram_2_data[6]), .pin4(ram_2_data[5]),
    .pin5(ram_2_data[4]), .pin6(ram_2_data[3]), .pin7(ram_2_data[2]), .pin8(ram_2_data[1]),
    .pin9(ram_2_data[0]), .pin19(n7474_1_pin5), .pin18(StackOut[15]), .pin17(StackOut[14]),
    .pin16(StackOut[13]), .pin15(StackOut[12]), .pin14(StackOut[11]), .pin13(StackOut[10]),
    .pin12(StackOut[9]), .pin11(StackOut[8]));
  // also tied to GND on the sheet: n74193_1_pin14
  // also tied to VCC on the sheet: n74193_1_pin11
endmodule

module ControlUnit (
  input  nStopHalt,
  input  ProgramLoad,
  input  clockEnable,
  input  notError,
  input  Clk,
  input  [15:0] DataBus,
  input  [15:0] ProgMemIn,
  input  [15:0] IRin,
  input  S0,
  input  S1,
  input  Load,
  output ClkOut,
  output RisingEdge,
  output FallingEdge,
  output AccClock,
  output Skip,
  output nClrIR,
  output VarWrite,
  output VarMemOut,
  output ProgMemOut,
  output StackOut,
  output StatusOut,
  output AccumulatorOut,
  output PortAOut,
  output PortBOut,
  output PortCOut,
  output PortDOut,
  output AccAllowInp
);

  wire n7400_1_pin1, n7400_1_pin3, n7400_1_pin11, n7400_2_pin6, n7400_2_pin8, n7400_2_pin11, n7400_4_pin3,
       n7400_4_pin6, n7400_4_pin11, n7400_4_pin12, n7408_1_pin6, n7408_2_pin3, n7408_2_pin6, n7408_3_pin3,
       n7408_3_pin6, n7408_3_pin8, n7408_3_pin11, n7408_5_pin11, n7408_7_pin3, n7408_7_pin6, n7414_1_pin1,
       n7414_1_pin2, n7414_1_pin4, n7414_1_pin6, n7414_1_pin8, n7414_1_pin10, n7414_1_pin13, n7414_2_pin8,
       n7414_2_pin10, n7414_2_pin12, n7414_3_pin2, n7414_3_pin4, n7432_1_pin3, n7432_1_pin6, n7432_1_pin11,
       n7432_5_pin8, n7432_5_pin11, n7442_1_pin1, n7442_1_pin2, n7442_1_pin3, n7442_1_pin4, n7474_1_pin4,
       n7474_1_pin5, n7474_1_pin6, n7486_1_pin11, n7486_1_pin12, n74151_1_pin5;

  _7442 #(.ShowInternalStructure("true")) u_7442_1 (
    .pin1(n7442_1_pin1), .pin2(n7442_1_pin2), .pin3(n7442_1_pin3), .pin4(n7442_1_pin4), .pin15(IRin[6]),
    .pin14(IRin[7]), .pin13(n7442_1_pin1), .pin12(n7442_1_pin1));  // open: pin5, pin6, pin7, pin11, pin10, pin9
  _7414 #(.ShowInternalStructure("true")) u_7414_1 (
    .pin1(n7414_1_pin1), .pin2(n7414_1_pin2), .pin3(n7414_1_pin2), .pin4(n7414_1_pin4), .pin5(n7414_1_pin4),
    .pin6(n7414_1_pin6), .pin13(n7414_1_pin13), .pin12(n7414_1_pin1), .pin11(n7414_1_pin1),
    .pin10(n7414_1_pin10), .pin9(n7414_1_pin10), .pin8(n7414_1_pin8));
  _7486 #(.ShowInternalStructure("true")) u_7486_1 (
    .pin13(IRin[0]), .pin12(n7486_1_pin12), .pin11(n7486_1_pin11));  // open: pin1, pin2, pin3, pin4, pin5, pin6, pin10, pin9, pin8
  _7408 #(.ShowInternalStructure("true")) u_7408_1 (
    .pin1(n7414_1_pin6), .pin2(n7414_1_pin1), .pin3(FallingEdge), .pin4(notError), .pin5(Clk),
    .pin6(n7408_1_pin6), .pin13(n7414_1_pin8), .pin12(n7414_1_pin13), .pin11(RisingEdge),
    .pin10(n7408_1_pin6), .pin9(clockEnable), .pin8(n7414_1_pin13));
  _7432 #(.ShowInternalStructure("true")) u_7432_1 (
    .pin1(IRin[2]), .pin2(IRin[3]), .pin3(n7432_1_pin3), .pin4(n7432_1_pin3), .pin5(IRin[4]),
    .pin6(n7432_1_pin6), .pin13(n7432_1_pin6), .pin12(IRin[1]), .pin11(n7432_1_pin11));  // open: pin10, pin9, pin8
  _7432 #(.ShowInternalStructure("true")) u_7432_2 (
    .pin1(S0), .pin2(n7442_1_pin4), .pin3(PortAOut), .pin4(S0), .pin5(n7442_1_pin3), .pin6(PortBOut),
    .pin13(S0), .pin12(n7442_1_pin2), .pin11(PortCOut), .pin10(S0), .pin9(n7442_1_pin1), .pin8(PortDOut));
  _7400 #(.ShowInternalStructure("true")) u_7400_1 (
    .pin1(n7400_1_pin1), .pin2(n7400_1_pin1), .pin3(n7400_1_pin3), .pin13(IRin[8]), .pin12(IRin[8]),
    .pin11(n7400_1_pin11), .pin10(n7400_1_pin11), .pin9(IRin[3]), .pin8(n7400_1_pin1));  // open: pin4, pin5, pin6
  _7474 #(.ShowInternalStructure("true")) u_7474_1 (
    .pin1(nStopHalt), .pin4(n7474_1_pin4), .pin5(n7474_1_pin5), .pin6(n7474_1_pin6));  // open: pin2, pin3, pin13, pin12, pin11, pin10, pin9, pin8
  _7400 #(.ShowInternalStructure("true")) u_7400_2 (
    .pin4(Load), .pin5(Load), .pin6(n7400_2_pin6), .pin13(n7432_1_pin11), .pin12(n7432_1_pin11),
    .pin11(n7400_2_pin11), .pin10(n7400_2_pin11), .pin9(IRin[0]), .pin8(n7400_2_pin8));  // open: pin1, pin2, pin3
  _7408 #(.ShowInternalStructure("true")) u_7408_2 (
    .pin1(IRin[4]), .pin2(IRin[1]), .pin3(n7408_2_pin3), .pin4(n7408_2_pin3), .pin5(S1), .pin6(n7408_2_pin6));  // open: pin13, pin12, pin11, pin10, pin9, pin8
  _74151 #(.ShowInternalStructure("true")) u_74151_1 (
    .pin1(DataBus[3]), .pin2(DataBus[2]), .pin3(DataBus[1]), .pin4(DataBus[0]), .pin5(n74151_1_pin5),
    .pin7(n7400_1_pin3), .pin15(DataBus[4]), .pin14(DataBus[5]), .pin13(DataBus[6]), .pin12(DataBus[7]),
    .pin11(ProgMemIn[0]), .pin10(ProgMemIn[1]), .pin9(ProgMemIn[2]));  // open: pin6
  _7432 #(.ShowInternalStructure("true")) u_7432_3 (
    .pin13(n7400_2_pin8), .pin12(n7474_1_pin5), .pin11(n7474_1_pin4));  // open: pin1, pin2, pin3, pin4, pin5, pin6, pin10, pin9, pin8
  _7414 #(.ShowInternalStructure("true")) u_7414_2 (
    .pin13(S0), .pin12(n7414_2_pin12), .pin11(n7414_2_pin12), .pin10(n7414_2_pin10), .pin9(n7414_2_pin10),
    .pin8(n7414_2_pin8));  // open: pin1, pin2, pin3, pin4, pin5, pin6
  _7400 #(.ShowInternalStructure("true")) u_7400_3 (
    .pin1(n7408_2_pin6), .pin2(n7408_2_pin6), .pin3(StatusOut), .pin13(IRin[8]), .pin12(IRin[8]),
    .pin11(n7442_1_pin1), .pin10(S1), .pin9(IRin[14]), .pin8(VarMemOut));  // open: pin4, pin5, pin6
  _7408 #(.ShowInternalStructure("true")) u_7408_3 (
    .pin1(FallingEdge), .pin2(IRin[10]), .pin3(n7408_3_pin3), .pin4(n7408_3_pin3), .pin5(S1),
    .pin6(n7408_3_pin6), .pin13(n7414_2_pin8), .pin12(S0), .pin11(n7408_3_pin11), .pin10(n7408_3_pin11),
    .pin9(IRin[11]), .pin8(n7408_3_pin8));
  _7400 #(.ShowInternalStructure("true")) u_7400_4 (
    .pin1(n7400_1_pin3), .pin2(n7400_1_pin3), .pin3(n7400_4_pin3), .pin4(n7400_4_pin3), .pin5(n74151_1_pin5),
    .pin6(n7400_4_pin6), .pin13(n7400_1_pin3), .pin12(n7400_4_pin12), .pin11(n7400_4_pin11),
    .pin10(n7400_4_pin11), .pin9(n7400_4_pin6), .pin8(n7486_1_pin12));
  _7408 #(.ShowInternalStructure("true")) u_7408_4 (
    .pin1(n7474_1_pin4), .pin2(n7400_2_pin6), .pin3(nClrIR), .pin12(n7474_1_pin4));  // open: pin4, pin5, pin6, pin13, pin11, pin10, pin9, pin8
  _7408 #(.ShowInternalStructure("true")) u_7408_5 (
    .pin1(S1), .pin2(IRin[10]), .pin3(AccAllowInp), .pin13(IRin[15]), .pin12(S1), .pin11(n7408_5_pin11));  // open: pin4, pin5, pin6, pin10, pin9, pin8
  _7432 #(.ShowInternalStructure("true")) u_7432_4 (
    .pin1(n7408_3_pin8), .pin2(n7408_3_pin6), .pin3(AccClock));  // open: pin4, pin5, pin6, pin13, pin12, pin11, pin10, pin9, pin8
  _74151 #(.ShowInternalStructure("true")) u_74151_2 (
    .pin1(DataBus[11]), .pin2(DataBus[10]), .pin3(DataBus[9]), .pin4(DataBus[8]), .pin5(n7400_4_pin12),
    .pin7(n7400_4_pin3), .pin15(DataBus[12]), .pin14(DataBus[13]), .pin13(DataBus[14]), .pin12(DataBus[15]),
    .pin11(ProgMemIn[0]), .pin10(ProgMemIn[1]), .pin9(ProgMemIn[2]));  // open: pin6
  _7432 #(.ShowInternalStructure("true")) u_7432_5 (
    .pin13(n7408_5_pin11), .pin12(ProgramLoad), .pin11(n7432_5_pin11), .pin10(n7432_5_pin11), .pin9(S0),
    .pin8(n7432_5_pin8));  // open: pin1, pin2, pin3, pin4, pin5, pin6
  _7408 #(.ShowInternalStructure("true")) u_7408_6 (
    .pin4(n7414_1_pin13), .pin5(n7474_1_pin6), .pin6(ClkOut));  // open: pin1, pin2, pin3, pin13, pin12, pin11, pin10, pin9, pin8
  _7414 #(.ShowInternalStructure("true")) u_7414_3 (
    .pin1(IRin[2]), .pin2(n7414_3_pin2), .pin3(IRin[3]), .pin4(n7414_3_pin4));  // open: pin5, pin6, pin13, pin12, pin11, pin10, pin9, pin8
  _7400 #(.ShowInternalStructure("true")) u_7400_5 (
    .pin1(S1), .pin2(IRin[13]), .pin3(AccumulatorOut), .pin4(S1), .pin5(IRin[12]), .pin6(StackOut),
    .pin13(n7432_5_pin8), .pin12(n7432_5_pin8), .pin11(ProgMemOut), .pin10(S1), .pin9(IRin[9]),
    .pin8(VarWrite));
  _7408 #(.ShowInternalStructure("true")) u_7408_7 (
    .pin1(n7414_3_pin4), .pin2(n7414_3_pin2), .pin3(n7408_7_pin3), .pin4(n7408_7_pin3), .pin5(IRin[4]),
    .pin6(n7408_7_pin6), .pin13(n7408_7_pin6), .pin12(n7486_1_pin11), .pin11(Skip));  // open: pin10, pin9, pin8

  // Notes on the sheet:
  //   Clock Edge Detector
  //   Bit Tester
  //   Enable & Error Test
  //   Bus Controller
  //   Decoder
endmodule

module PPU (
  input  in_1,
  input  in_2,
  input  in_3,
  input  in_4
);

  wire comparator_1_eq, comparator_2_eq, comparator_3_eq, n74161_1_pin7, n74161_1_pin10, n74161_1_pin15,
       n74161_2_pin7, n74161_2_pin10, n74161_2_pin15, n74161_3_pin7, n74161_3_pin9, n74161_3_pin15,
       n74161_4_pin7, n74161_4_pin9, undriven;
  wire [3:0] n74161_1_pin14, n74161_3_pin14;

  _74161 #(.ShowInternalStructure("true")) u_74161_1 (
    .pin1(in_1), .pin2(in_2), .pin7(n74161_1_pin7), .pin15(n74161_1_pin15), .pin14(n74161_1_pin14[0]),
    .pin13(n74161_1_pin14[1]), .pin12(n74161_1_pin14[2]), .pin11(n74161_1_pin14[3]), .pin10(n74161_1_pin10),
    .pin9(n74161_1_pin10));  // open: pin3, pin4, pin5, pin6
  _74161 #(.ShowInternalStructure("true")) u_74161_2 (
    .pin1(in_3), .pin2(in_4), .pin7(n74161_2_pin7), .pin15(n74161_2_pin15), .pin10(n74161_2_pin10),
    .pin9(n74161_2_pin10));  // open: pin3, pin4, pin5, pin6, pin14, pin13, pin12, pin11
  _74161 #(.ShowInternalStructure("true")) u_74161_3 (
    .pin1(in_1), .pin2(in_2), .pin7(n74161_3_pin7), .pin15(n74161_3_pin15), .pin14(n74161_3_pin14[0]),
    .pin13(n74161_3_pin14[1]), .pin12(n74161_3_pin14[2]), .pin11(n74161_3_pin14[3]), .pin10(n74161_1_pin15),
    .pin9(n74161_3_pin9));  // open: pin3, pin4, pin5, pin6
  _74161 #(.ShowInternalStructure("true")) u_74161_4 (
    .pin1(in_3), .pin2(in_4), .pin7(n74161_4_pin7), .pin10(n74161_2_pin15), .pin9(n74161_4_pin9));  // open: pin3, pin4, pin5, pin6, pin15, pin14, pin13, pin12, pin11
  Comparator comparator_1 (.a({n74161_3_pin14, n74161_1_pin14}), .b(8'hd0), .eq(comparator_1_eq));  // open: gt, lt
  Comparator comparator_2 (.a({n74161_3_pin14, n74161_1_pin14}), .b(8'hce), .eq(comparator_2_eq));  // open: gt, lt
  Comparator comparator_3 (.a({n74161_3_pin14, n74161_1_pin14}), .b(8'he0), .eq(comparator_3_eq));  // open: gt, lt
  Comparator comparator_4 (.a({n74161_3_pin14, n74161_1_pin14}), .b(8'he0));  // open: gt, eq, lt
  D_Flip_Flop d_ff_1 (.preset(undriven), .reset(comparator_1_eq));  // open: D, clk, Q, Qn
  D_Flip_Flop d_ff_2 (.preset(comparator_3_eq), .reset(comparator_2_eq));  // open: D, clk, Q, Qn
  // also tied to VCC on the sheet: {n74161_1_pin10, n74161_1_pin7, n74161_2_pin10, n74161_2_pin7, n74161_3_pin7, n74161_4_pin7, n74161_3_pin9, n74161_4_pin9}
endmodule

module InstructionRegister (
  input  [15:0] DataBus,
  input  clk,
  input  nClearIR,
  output [15:0] DataOut
);

  _74273 #(.ShowInternalStructure("true")) u_74273_1 (
    .pin1(nClearIR), .pin2(DataOut[0]), .pin3(DataBus[0]), .pin4(DataBus[1]), .pin5(DataOut[1]),
    .pin6(DataOut[2]), .pin7(DataBus[2]), .pin8(DataBus[3]), .pin9(DataOut[3]), .pin19(DataOut[7]),
    .pin18(DataBus[7]), .pin17(DataBus[6]), .pin16(DataOut[6]), .pin15(DataOut[5]), .pin14(DataBus[5]),
    .pin13(DataBus[4]), .pin12(DataOut[4]), .pin11(clk));
  _7427 #(.ShowInternalStructure("true")) u_7427_1 ();  // open: pin1, pin2, pin3, pin4, pin5, pin6, pin13, pin12, pin11, pin10, pin9, pin8
  _7400 #(.ShowInternalStructure("true")) u_7400_1 ();  // open: pin1, pin2, pin3, pin4, pin5, pin6, pin13, pin12, pin11, pin10, pin9, pin8
  _74273 #(.ShowInternalStructure("true")) u_74273_2 (
    .pin1(nClearIR), .pin2(DataOut[8]), .pin3(DataBus[8]), .pin4(DataBus[9]), .pin5(DataOut[9]),
    .pin6(DataOut[10]), .pin7(DataBus[10]), .pin8(DataBus[11]), .pin9(DataOut[11]), .pin19(DataOut[15]),
    .pin18(DataBus[15]), .pin17(DataBus[14]), .pin16(DataOut[14]), .pin15(DataOut[13]), .pin14(DataBus[13]),
    .pin13(DataBus[12]), .pin12(DataOut[12]), .pin11(clk));

  // Notes on the sheet:
  //   nClearIR: initial=0x1
endmodule

module StatusRegister (
  input  IgnoreError,
  input  nSetError,
  input  SetSkip,
  input  nLoading,
  input  S0,
  input  SetZero,
  input  SetNegative,
  input  SetOverflow,
  input  SetUnderflow,
  input  SetAlessB,
  input  SetAisB,
  input  SetAgreatB,
  output nError,
  output Skip,
  output Zero,
  output Negative,
  output Overflow,
  output Underflow,
  output AlessB,
  output AisB,
  output AgreatB
);

  wire n7400_1_pin3, n7400_1_pin6, n7400_1_pin8, n7474_1_pin2, n74273_1_pin1;

  _7400 #(.ShowInternalStructure("true")) u_7400_1 (
    .pin1(nLoading), .pin2(nLoading), .pin3(n7400_1_pin3), .pin4(SetSkip), .pin5(nLoading),
    .pin6(n7400_1_pin6), .pin10(IgnoreError), .pin9(IgnoreError), .pin8(n7400_1_pin8));  // open: pin13, pin12, pin11
  _7474 #(.ShowInternalStructure("true")) u_7474_1 (
    .pin1(n7400_1_pin3), .pin2(n7474_1_pin2), .pin3(S0), .pin4(n7400_1_pin6), .pin5(Skip),
    .pin13(n7400_1_pin8), .pin10(nSetError), .pin8(nError));  // open: pin6, pin12, pin11, pin9
  _74273 #(.ShowInternalStructure("true")) u_74273_1 (
    .pin1(n74273_1_pin1), .pin2(Zero), .pin3(SetZero), .pin4(SetNegative), .pin5(Negative), .pin6(Overflow),
    .pin7(SetOverflow), .pin8(SetUnderflow), .pin9(Underflow), .pin17(SetAgreatB), .pin16(AgreatB),
    .pin15(AisB), .pin14(SetAisB), .pin13(SetAlessB), .pin12(AlessB), .pin11(S0));  // open: pin19, pin18
  // also tied to GND on the sheet: n7474_1_pin2
  // also tied to VCC on the sheet: n74273_1_pin1
endmodule

module OutputPortA (
  input  [15:0] DataBus,
  input  [15:0] InstructionRegister,
  input  S1,
  input  Clock,
  output [15:0] PortOutput
);

  wire n7408_1_pin1, n7408_1_pin3, n7408_1_pin6, n7408_1_pin11, n7414_1_pin6, n7442_1_pin2, n7442_1_pin13,
       n74273_1_pin1;

  _7442 #(.ShowInternalStructure("true")) u_7442_1 (
    .pin2(n7442_1_pin2), .pin15(InstructionRegister[7]), .pin14(InstructionRegister[6]),
    .pin13(n7442_1_pin13), .pin12(n7442_1_pin13));  // open: pin1, pin3, pin4, pin5, pin6, pin7, pin11, pin10, pin9
  _7414 #(.ShowInternalStructure("true")) u_7414_1 (
    .pin5(Clock), .pin6(n7414_1_pin6));  // open: pin1, pin2, pin3, pin4, pin13, pin12, pin11, pin10, pin9, pin8
  _7408 #(.ShowInternalStructure("true")) u_7408_1 (
    .pin1(n7408_1_pin1), .pin2(S1), .pin3(n7408_1_pin3), .pin4(n7408_1_pin3), .pin5(n7414_1_pin6),
    .pin6(n7408_1_pin6), .pin13(n7442_1_pin2), .pin12(InstructionRegister[2]), .pin11(n7408_1_pin11),
    .pin10(n7408_1_pin11), .pin9(InstructionRegister[0]), .pin8(n7408_1_pin1));
  _74273 #(.ShowInternalStructure("true")) u_74273_1 (
    .pin1(n74273_1_pin1), .pin2(PortOutput[0]), .pin3(DataBus[15]), .pin4(DataBus[14]), .pin5(PortOutput[1]),
    .pin6(PortOutput[2]), .pin7(DataBus[13]), .pin8(DataBus[12]), .pin9(PortOutput[3]),
    .pin19(PortOutput[7]), .pin18(DataBus[8]), .pin17(DataBus[9]), .pin16(PortOutput[6]),
    .pin15(PortOutput[5]), .pin14(DataBus[10]), .pin13(DataBus[11]), .pin12(PortOutput[4]),
    .pin11(n7408_1_pin6));
  _74273 #(.ShowInternalStructure("true")) u_74273_2 (
    .pin1(n74273_1_pin1), .pin2(PortOutput[8]), .pin3(DataBus[7]), .pin4(DataBus[6]), .pin5(PortOutput[9]),
    .pin6(PortOutput[10]), .pin7(DataBus[5]), .pin8(DataBus[4]), .pin9(PortOutput[11]),
    .pin19(PortOutput[15]), .pin18(DataBus[0]), .pin17(DataBus[1]), .pin16(PortOutput[14]),
    .pin15(PortOutput[13]), .pin14(DataBus[2]), .pin13(DataBus[3]), .pin12(PortOutput[12]),
    .pin11(n7408_1_pin6));
  // also tied to GND on the sheet: n7442_1_pin13
  // also tied to VCC on the sheet: n74273_1_pin1
endmodule

module OutputPortB (
  input  [15:0] DataBus,
  input  [15:0] InstructionRegister,
  input  S1,
  input  Clock,
  output [15:0] PortOutput
);

  wire n7408_1_pin1, n7408_1_pin3, n7408_1_pin6, n7408_1_pin11, n7414_1_pin6, n7442_1_pin1, n7442_1_pin13,
       n74273_1_pin1;

  _7442 #(.ShowInternalStructure("true")) u_7442_1 (
    .pin1(n7442_1_pin1), .pin15(InstructionRegister[7]), .pin14(InstructionRegister[6]),
    .pin13(n7442_1_pin13), .pin12(n7442_1_pin13));  // open: pin2, pin3, pin4, pin5, pin6, pin7, pin11, pin10, pin9
  _7414 #(.ShowInternalStructure("true")) u_7414_1 (
    .pin5(Clock), .pin6(n7414_1_pin6));  // open: pin1, pin2, pin3, pin4, pin13, pin12, pin11, pin10, pin9, pin8
  _7408 #(.ShowInternalStructure("true")) u_7408_1 (
    .pin1(n7408_1_pin1), .pin2(S1), .pin3(n7408_1_pin3), .pin4(n7408_1_pin3), .pin5(n7414_1_pin6),
    .pin6(n7408_1_pin6), .pin13(n7442_1_pin1), .pin12(InstructionRegister[2]), .pin11(n7408_1_pin11),
    .pin10(n7408_1_pin11), .pin9(InstructionRegister[0]), .pin8(n7408_1_pin1));
  _74273 #(.ShowInternalStructure("true")) u_74273_1 (
    .pin1(n74273_1_pin1), .pin2(PortOutput[0]), .pin3(DataBus[15]), .pin4(DataBus[14]), .pin5(PortOutput[1]),
    .pin6(PortOutput[2]), .pin7(DataBus[13]), .pin8(DataBus[12]), .pin9(PortOutput[3]),
    .pin19(PortOutput[7]), .pin18(DataBus[8]), .pin17(DataBus[9]), .pin16(PortOutput[6]),
    .pin15(PortOutput[5]), .pin14(DataBus[10]), .pin13(DataBus[11]), .pin12(PortOutput[4]),
    .pin11(n7408_1_pin6));
  _74273 #(.ShowInternalStructure("true")) u_74273_2 (
    .pin1(n74273_1_pin1), .pin2(PortOutput[8]), .pin3(DataBus[7]), .pin4(DataBus[6]), .pin5(PortOutput[9]),
    .pin6(PortOutput[10]), .pin7(DataBus[5]), .pin8(DataBus[4]), .pin9(PortOutput[11]),
    .pin19(PortOutput[15]), .pin18(DataBus[0]), .pin17(DataBus[1]), .pin16(PortOutput[14]),
    .pin15(PortOutput[13]), .pin14(DataBus[2]), .pin13(DataBus[3]), .pin12(PortOutput[12]),
    .pin11(n7408_1_pin6));
  // also tied to GND on the sheet: n7442_1_pin13
  // also tied to VCC on the sheet: n74273_1_pin1
endmodule

module JumpManager (
  input  S1,
  input  CLK,
  input  [15:0] InstructionRegister,
  output PC_Jump,
  output Stack_Push,
  output Stack_Pop,
  output PC_Return
);

  wire n7400_1_pin3, n7400_1_pin6, n7400_1_pin11, n7400_2_pin3, n7400_2_pin8, n7400_2_pin11, n7408_1_pin3,
       n7408_1_pin11, n7408_2_pin3, n7408_2_pin11, n7432_1_pin11, n7442_1_pin3, n7442_1_pin4, n7442_1_pin7;

  _7432 #(.ShowInternalStructure("true")) u_7432_1 (
    .pin13(InstructionRegister[4]), .pin12(InstructionRegister[3]), .pin11(n7432_1_pin11));  // open: pin1, pin2, pin3, pin4, pin5, pin6, pin10, pin9, pin8
  _7442 #(.ShowInternalStructure("true")) u_7442_1 (
    .pin3(n7442_1_pin3), .pin4(n7442_1_pin4), .pin7(n7442_1_pin7), .pin15(InstructionRegister[0]),
    .pin14(InstructionRegister[1]), .pin13(InstructionRegister[2]), .pin12(n7432_1_pin11));  // open: pin1, pin2, pin5, pin6, pin11, pin10, pin9
  _7400 #(.ShowInternalStructure("true")) u_7400_1 (
    .pin1(n7442_1_pin4), .pin2(n7442_1_pin4), .pin3(n7400_1_pin3), .pin4(CLK), .pin5(CLK),
    .pin6(n7400_1_pin6), .pin13(n7442_1_pin4), .pin12(n7442_1_pin4), .pin11(n7400_1_pin11));  // open: pin10, pin9, pin8
  _7400 #(.ShowInternalStructure("true")) u_7400_2 (
    .pin1(n7442_1_pin3), .pin2(n7442_1_pin3), .pin3(n7400_2_pin3), .pin13(n7442_1_pin3),
    .pin12(n7442_1_pin7), .pin11(n7400_2_pin11), .pin10(CLK), .pin9(CLK), .pin8(n7400_2_pin8));  // open: pin4, pin5, pin6
  _7408 #(.ShowInternalStructure("true")) u_7408_1 (
    .pin1(n7400_1_pin6), .pin2(n7400_1_pin3), .pin3(n7408_1_pin3), .pin4(n7408_1_pin3), .pin5(S1),
    .pin6(PC_Return), .pin13(n7400_1_pin11), .pin12(S1), .pin11(n7408_1_pin11), .pin10(n7408_1_pin11),
    .pin9(CLK), .pin8(Stack_Pop));
  _7408 #(.ShowInternalStructure("true")) u_7408_2 (
    .pin1(n7400_2_pin3), .pin2(S1), .pin3(n7408_2_pin3), .pin4(n7408_2_pin3), .pin5(CLK), .pin6(Stack_Push),
    .pin13(n7400_2_pin8), .pin12(n7400_2_pin11), .pin11(n7408_2_pin11), .pin10(n7408_2_pin11), .pin9(S1),
    .pin8(PC_Jump));

  // Notes on the sheet:
  //   Stack Pop Manager
  //   PC Return Manager
  //   PC Call/Jump Manager
  //   Stack Push Manager
endmodule
