// Logisim project NewCPU.circ as structural Verilog
module main (
);

  ProgramCounter programcounter_1 ();  // open: PulseIn, NextInst, out_3
  ROMmanager rommanager_1 ();  // open: AddressIn, MSByteOut, LSByteOut
endmodule

module ALUx8 (
  input  [7:0] Ain,
  input  [7:0] Bin,
  input  [2:0] Inst,
  input  Cin,
  output Pn,
  output Cn,
  output [7:0] Qout,
  output Zero
);

  wire n7414_1_pin1, n7414_1_pin2, n7432_1_pin3, n7432_1_pin6, n7432_1_pin8, n7432_1_pin11, n7432_2_pin3,
       n7432_2_pin5, n7432_2_pin6;

  // _74381 #(.ShowInternalStructure("true")) 74381_1: pin names not known; wires that end beside it: Ain[1], Ain[2], Bin[1], Bin[2], Ain[0], Ain[3], Bin[0], Bin[3], Inst[0], Cin, Inst[1]
  _7414 #(.ShowInternalStructure("true")) u_7414_1 (
    .pin1(n7414_1_pin1), .pin2(n7414_1_pin2));  // open: pin3, pin4, pin5, pin6, pin13, pin12, pin11, pin10, pin9, pin8
  // _74381 #(.ShowInternalStructure("true")) 74381_2: pin names not known; wires that end beside it: Inst[2], n7414_1_pin1, Qout[0], Qout[3], Qout[1], Qout[2], Ain[5], Ain[6], Bin[5], Bin[6], Ain[4], Ain[7], Bin[4], Bin[7], Inst[0], n7414_1_pin2, Inst[1], Pn, Inst[2], Cn, Qout[4], Qout[7], Qout[5], Qout[6]
  _7432 #(.ShowInternalStructure("true")) u_7432_1 (
    .pin1(Qout[4]), .pin2(Qout[5]), .pin3(n7432_1_pin3), .pin4(Qout[6]), .pin5(Qout[7]), .pin6(n7432_1_pin6),
    .pin13(Qout[3]), .pin12(Qout[2]), .pin11(n7432_1_pin11), .pin10(Qout[1]), .pin9(Qout[0]),
    .pin8(n7432_1_pin8));
  _7432 #(.ShowInternalStructure("true")) u_7432_2 (
    .pin1(n7432_1_pin6), .pin2(n7432_1_pin3), .pin3(n7432_2_pin3), .pin4(n7432_2_pin3), .pin5(n7432_2_pin5),
    .pin6(n7432_2_pin6), .pin13(n7432_1_pin8), .pin12(n7432_1_pin11), .pin11(n7432_2_pin5));  // open: pin10, pin9, pin8
  _7414 #(.ShowInternalStructure("true")) u_7414_2 (
    .pin13(n7432_2_pin6), .pin12(Zero));  // open: pin1, pin2, pin3, pin4, pin5, pin6, pin11, pin10, pin9, pin8
endmodule

module ProgramCounter (
  input  PulseIn,
  input  NextInst,
  output [7:0] out_3
);

  wire n74193_1_pin7, n74193_1_pin14, n74193_2_pin12, n74193_3_pin12, n74283_1_pin9, n74283_2_pin9;
  wire [2:0] n74193_1_pin3;
  wire [3:0] n74193_2_pin3, n74193_3_pin3, n74193_4_pin3;

  _74193 #(.ShowInternalStructure("true")) u_74193_1 (
    .pin2(n74193_1_pin3[1]), .pin3(n74193_1_pin3[0]), .pin5(PulseIn), .pin6(n74193_1_pin3[2]),
    .pin7(n74193_1_pin7), .pin14(n74193_1_pin14));  // open: pin1, pin4, pin15, pin13, pin12, pin11, pin10, pin9
  _7432 #(.ShowInternalStructure("true")) u_7432_1 (
    .pin1(n74193_1_pin7), .pin2(NextInst), .pin3(n74193_1_pin14));  // open: pin4, pin5, pin6, pin13, pin12, pin11, pin10, pin9, pin8
  _74193 #(.ShowInternalStructure("true")) u_74193_2 (
    .pin2(n74193_2_pin3[1]), .pin3(n74193_2_pin3[0]), .pin5(n74193_1_pin14), .pin6(n74193_2_pin3[2]),
    .pin7(n74193_2_pin3[3]), .pin12(n74193_2_pin12));  // open: pin1, pin4, pin15, pin14, pin13, pin11, pin10, pin9
  _74283 #(.ShowInternalStructure("true")) u_74283_1 (
    .pin1(out_3[1]), .pin3(n74193_2_pin3[1]), .pin4(out_3[0]), .pin5(n74193_2_pin3[0]),
    .pin14(n74193_2_pin3[2]), .pin13(out_3[2]), .pin12(n74193_2_pin3[3]), .pin10(out_3[3]),
    .pin9(n74283_1_pin9));  // open: pin2, pin6, pin7, pin15, pin11
  _74193 #(.ShowInternalStructure("true")) u_74193_3 (
    .pin2(n74193_3_pin3[1]), .pin3(n74193_3_pin3[0]), .pin5(n74193_2_pin12), .pin6(n74193_3_pin3[2]),
    .pin7(n74193_3_pin3[3]), .pin12(n74193_3_pin12));  // open: pin1, pin4, pin15, pin14, pin13, pin11, pin10, pin9
  _74283 #(.ShowInternalStructure("true")) u_74283_2 (
    .pin1(out_3[5]), .pin3(n74193_3_pin3[1]), .pin4(out_3[4]), .pin5(n74193_3_pin3[0]), .pin7(n74283_1_pin9),
    .pin14(n74193_3_pin3[2]), .pin13(out_3[6]), .pin12(n74193_3_pin3[3]), .pin10(out_3[7]),
    .pin9(n74283_2_pin9));  // open: pin2, pin6, pin15, pin11
  _74193 #(.ShowInternalStructure("true")) u_74193_4 (
    .pin2(n74193_4_pin3[1]), .pin3(n74193_4_pin3[0]), .pin5(n74193_3_pin12), .pin6(n74193_4_pin3[2]),
    .pin7(n74193_4_pin3[3]));  // open: pin1, pin4, pin15, pin14, pin13, pin12, pin11, pin10, pin9
  _74283 #(.ShowInternalStructure("true")) u_74283_3 (
    .pin3(n74193_4_pin3[1]), .pin5(n74193_4_pin3[0]), .pin7(n74283_2_pin9), .pin14(n74193_4_pin3[2]),
    .pin12(n74193_4_pin3[3]));  // open: pin1, pin2, pin4, pin6, pin15, pin13, pin11, pin10, pin9

  // Notes on the sheet:
  //   Step Counter
  //   Line Counter
endmodule

module TWOxTWObyteShiftRegister (
  input  ShftByt,
  input  nCLR,
  input  [7:0] Din,
  output [7:0] ByteA,
  output [7:0] ByteB
);

  _74273 #(.ShowInternalStructure("true")) u_74273_1 (
    .pin1(nCLR), .pin2(ByteA[0]), .pin3(Din[0]), .pin4(Din[1]), .pin5(ByteA[1]), .pin6(ByteA[2]),
    .pin7(Din[2]), .pin8(Din[3]), .pin9(ByteA[3]), .pin19(ByteA[7]), .pin18(Din[7]), .pin17(Din[6]),
    .pin16(ByteA[6]), .pin15(ByteA[5]), .pin14(Din[5]), .pin13(Din[4]), .pin12(ByteA[4]), .pin11(ShftByt));
  _74273 #(.ShowInternalStructure("true")) u_74273_2 (
    .pin1(nCLR), .pin2(ByteB[0]), .pin3(ByteA[0]), .pin4(ByteA[1]), .pin5(ByteB[1]), .pin6(ByteB[2]),
    .pin7(ByteA[2]), .pin8(ByteA[3]), .pin9(ByteB[3]), .pin19(ByteB[7]), .pin18(ByteA[7]), .pin17(ByteA[6]),
    .pin16(ByteB[6]), .pin15(ByteB[5]), .pin14(ByteA[5]), .pin13(ByteA[4]), .pin12(ByteB[4]), .pin11(ShftByt));
endmodule

module InstructionDecoder (
  input  [15:0] in_1,
  output enALU
);

  wire l_74154_e6f28a0a_2_y0, n7432_1_pin8, n7432_1_pin9, n7432_1_pin11, n7432_1_pin12;

  L_74154_e6f28a0a l_74154_e6f28a0a_1 (
    .iE0(1'b0), .iE1(1'b0), .A0(in_1[3]), .A1(in_1[2]), .A2(in_1[1]), .A3(in_1[0]));  // open: Y3, Y4, Y5, Y6, Y7, Y8, Y9, Y10, Y11, Y12, Y13, Y14, Y15, Y0, Y1, Y2
  L_74154_e6f28a0a l_74154_e6f28a0a_2 (
    .iE0(1'b0), .iE1(1'b0), .A0(in_1[7]), .A1(in_1[6]), .A2(in_1[5]), .A3(in_1[4]), .Y0(l_74154_e6f28a0a_2_y0));  // open: Y3, Y4, Y5, Y6, Y7, Y8, Y9, Y10, Y11, Y12, Y13, Y14, Y15, Y1, Y2
  _7432 #(.ShowInternalStructure("true")) u_7432_1 (
    .pin13(l_74154_e6f28a0a_2_y0), .pin12(n7432_1_pin12), .pin11(n7432_1_pin11), .pin10(n7432_1_pin11),
    .pin9(n7432_1_pin9), .pin8(n7432_1_pin8));  // open: pin1, pin2, pin3, pin4, pin5, pin6
  _7400 #(.ShowInternalStructure("true")) u_7400_1 (
    .pin13(n7432_1_pin8), .pin12(n7432_1_pin8), .pin11(enALU));  // open: pin1, pin2, pin3, pin4, pin5, pin6, pin10, pin9, pin8
  L_74154_e6f28a0a l_74154_e6f28a0a_3 (
    .iE0(1'b0), .iE1(1'b0), .A0(in_1[11]), .A1(in_1[10]), .A2(in_1[9]), .A3(in_1[8]), .Y0(n7432_1_pin12));  // open: Y3, Y4, Y5, Y6, Y7, Y8, Y9, Y10, Y11, Y12, Y13, Y14, Y15, Y1, Y2
  L_74154_e6f28a0a l_74154_e6f28a0a_4 (
    .iE0(1'b0), .iE1(1'b0), .A0(in_1[15]), .A1(in_1[14]), .A2(in_1[13]), .A3(in_1[12]), .Y0(n7432_1_pin9));  // open: Y3, Y4, Y5, Y6, Y7, Y8, Y9, Y10, Y11, Y12, Y13, Y14, Y15, Y1, Y2
endmodule

module JumpStack (
  input  StackPop,
  input  StackPush
);

  wire n7485_1_pin1, n7485_1_pin2, n74193_1_pin2, n74193_1_pin3, n74193_1_pin6, n74193_1_pin7, not_1_out,
       not_2_out, StackIn_pin1, StackOut_pin1;
  wire [7:0] ram_1_data, StackIn_pin9, undriven;

  _74193 #(.ShowInternalStructure("true")) u_74193_1 (
    .pin2(n74193_1_pin2), .pin3(n74193_1_pin3), .pin6(n74193_1_pin6), .pin7(n74193_1_pin7));  // open: pin1, pin4, pin5, pin15, pin14, pin13, pin12, pin11, pin10, pin9
  _74193 #(.ShowInternalStructure("true")) u_74193_2 ();  // open: pin1, pin2, pin3, pin4, pin5, pin6, pin7, pin15, pin14, pin13, pin12, pin11, pin10, pin9
  _7485 #(.ShowInternalStructure("true")) u_7485_1 (
    .pin1(n7485_1_pin1), .pin2(n7485_1_pin2), .pin4(n7485_1_pin2), .pin15(n74193_1_pin7),
    .pin14(n7485_1_pin1), .pin13(n74193_1_pin6), .pin12(n74193_1_pin2), .pin11(n7485_1_pin1),
    .pin10(n74193_1_pin3), .pin9(n7485_1_pin1));  // open: pin3, pin5, pin6, pin7
  RAM #(.databus("bidir"), .trigger("high")) ram_1 (.addr(undriven), .we(not_1_out), .oe(not_2_out), .data(ram_1_data));
  // NOT_Gate not_1 has open pins: in=open, out=not_1_out
  // NOT_Gate not_2 has open pins: in=open, out=not_2_out
  _7474 #(.ShowInternalStructure("true")) u_7474_1 ();  // open: pin1, pin2, pin3, pin4, pin5, pin6, pin13, pin12, pin11, pin10, pin9, pin8
  _74541 #(.ShowInternalStructure("true")) StackIn (
    .pin1(StackIn_pin1), .pin2(StackIn_pin9[7]), .pin3(StackIn_pin9[6]), .pin4(StackIn_pin9[5]),
    .pin5(StackIn_pin9[4]), .pin6(StackIn_pin9[3]), .pin7(StackIn_pin9[2]), .pin8(StackIn_pin9[1]),
    .pin9(StackIn_pin9[0]), .pin19(StackIn_pin1), .pin18(ram_1_data[7]), .pin17(ram_1_data[6]),
    .pin16(ram_1_data[5]), .pin15(ram_1_data[4]), .pin14(ram_1_data[3]), .pin13(ram_1_data[2]),
    .pin12(ram_1_data[1]), .pin11(ram_1_data[0]));
  _74541 #(.ShowInternalStructure("true")) StackOut (
    .pin1(StackOut_pin1), .pin2(ram_1_data[7]), .pin3(ram_1_data[6]), .pin4(ram_1_data[5]),
    .pin5(ram_1_data[4]), .pin6(ram_1_data[3]), .pin7(ram_1_data[2]), .pin8(ram_1_data[1]),
    .pin9(ram_1_data[0]), .pin19(StackOut_pin1));  // open: pin18, pin17, pin16, pin15, pin14, pin13, pin12, pin11
endmodule

module DoublePulseGenerator (
  input  PulseIn,
  output PulseOut
);

  wire n7408_1_pin3, n7408_1_pin11, n7414_1_pin1, n7414_1_pin2, n7414_1_pin4, n7414_1_pin6, n7414_1_pin8,
       n7414_1_pin10;

  _7414 #(.ShowInternalStructure("true")) u_7414_1 (
    .pin1(n7414_1_pin1), .pin2(n7414_1_pin2), .pin3(n7414_1_pin2), .pin4(n7414_1_pin4), .pin5(n7414_1_pin4),
    .pin6(n7414_1_pin6), .pin13(PulseIn), .pin12(n7414_1_pin1), .pin11(n7414_1_pin1), .pin10(n7414_1_pin10),
    .pin9(n7414_1_pin10), .pin8(n7414_1_pin8));
  _7408 #(.ShowInternalStructure("true")) u_7408_1 (
    .pin1(n7414_1_pin6), .pin2(n7414_1_pin1), .pin3(n7408_1_pin3), .pin13(n7414_1_pin8), .pin12(PulseIn),
    .pin11(n7408_1_pin11));  // open: pin4, pin5, pin6, pin10, pin9, pin8
  _7432 #(.ShowInternalStructure("true")) u_7432_1 (
    .pin13(n7408_1_pin3), .pin12(n7408_1_pin11), .pin11(PulseOut));  // open: pin1, pin2, pin3, pin4, pin5, pin6, pin10, pin9, pin8
endmodule

module Registers (
  input  [7:0] ByteA,
  input  [7:0] ByteB,
  input  ClearAll,
  input  InstructionClk,
  input  InputAClk,
  input  InputBClk,
  output [7:0] Instruction,
  output [7:0] InputFlags,
  output [7:0] DataAMSByte,
  output [7:0] DataALSByte,
  output [7:0] DataBMSByte,
  output [7:0] DataBLSByte
);

  _74273 #(.ShowInternalStructure("true")) u_74273_1 (
    .pin1(ClearAll), .pin2(Instruction[4]), .pin3(ByteA[4]), .pin4(ByteA[5]), .pin5(Instruction[5]),
    .pin6(Instruction[6]), .pin7(ByteA[6]), .pin8(ByteA[7]), .pin9(Instruction[7]), .pin19(Instruction[3]),
    .pin18(ByteA[3]), .pin17(ByteA[2]), .pin16(Instruction[2]), .pin15(Instruction[1]), .pin14(ByteA[1]),
    .pin13(ByteA[0]), .pin12(Instruction[0]), .pin11(InstructionClk));
  _74273 #(.ShowInternalStructure("true")) u_74273_2 (
    .pin1(ClearAll), .pin2(InputFlags[4]), .pin3(ByteB[4]), .pin4(ByteB[5]), .pin5(InputFlags[5]),
    .pin6(InputFlags[6]), .pin7(ByteB[6]), .pin8(ByteB[7]), .pin9(InputFlags[7]), .pin19(InputFlags[3]),
    .pin18(ByteB[3]), .pin17(ByteB[2]), .pin16(InputFlags[2]), .pin15(InputFlags[1]), .pin14(ByteB[1]),
    .pin13(ByteB[0]), .pin12(InputFlags[0]), .pin11(InstructionClk));
  _74273 #(.ShowInternalStructure("true")) u_74273_3 (
    .pin1(ClearAll), .pin2(DataAMSByte[4]), .pin3(ByteA[4]), .pin4(ByteA[5]), .pin5(DataAMSByte[5]),
    .pin6(DataAMSByte[6]), .pin7(ByteA[6]), .pin8(ByteA[7]), .pin9(DataAMSByte[7]), .pin19(DataAMSByte[3]),
    .pin18(ByteA[3]), .pin17(ByteA[2]), .pin16(DataAMSByte[2]), .pin15(DataAMSByte[1]), .pin14(ByteA[1]),
    .pin13(ByteA[0]), .pin12(DataAMSByte[0]), .pin11(InputAClk));
  _74273 #(.ShowInternalStructure("true")) u_74273_4 (
    .pin1(ClearAll), .pin2(DataALSByte[4]), .pin3(ByteB[4]), .pin4(ByteB[5]), .pin5(DataALSByte[5]),
    .pin6(DataALSByte[6]), .pin7(ByteB[6]), .pin8(ByteB[7]), .pin9(DataALSByte[7]), .pin19(DataALSByte[3]),
    .pin18(ByteB[3]), .pin17(ByteB[2]), .pin16(DataALSByte[2]), .pin15(DataALSByte[1]), .pin14(ByteB[1]),
    .pin13(ByteB[0]), .pin12(DataALSByte[0]), .pin11(InputAClk));
  _74273 #(.ShowInternalStructure("true")) u_74273_5 (
    .pin1(ClearAll), .pin2(DataBMSByte[4]), .pin3(ByteA[4]), .pin4(ByteA[5]), .pin5(DataBMSByte[5]),
    .pin6(DataBMSByte[6]), .pin7(ByteA[6]), .pin8(ByteA[7]), .pin9(DataBMSByte[7]), .pin19(DataBMSByte[3]),
    .pin18(ByteA[3]), .pin17(ByteA[2]), .pin16(DataBMSByte[2]), .pin15(DataBMSByte[1]), .pin14(ByteA[1]),
    .pin13(ByteA[0]), .pin12(DataBMSByte[0]), .pin11(InputBClk));
  _74273 #(.ShowInternalStructure("true")) u_74273_6 (
    .pin1(ClearAll), .pin2(DataBLSByte[4]), .pin3(ByteB[4]), .pin4(ByteB[5]), .pin5(DataBLSByte[5]),
    .pin6(DataBLSByte[6]), .pin7(ByteB[6]), .pin8(ByteB[7]), .pin9(DataBLSByte[7]), .pin19(DataBLSByte[3]),
    .pin18(ByteB[3]), .pin17(ByteB[2]), .pin16(DataBLSByte[2]), .pin15(DataBLSByte[1]), .pin14(ByteB[1]),
    .pin13(ByteB[0]), .pin12(DataBLSByte[0]), .pin11(InputBClk));

  // Notes on the sheet:
  //   InputFlags
  //   Instruction
  //   Input A LSByte
  //   Input A MSByte
  //   Input B  MSByte
  //   Input B LSByte
endmodule

module ALUx16 (
  input  [7:0] MSByteAIn,
  input  [7:0] MSByteBin,
  input  [7:0] LSByteAIn,
  input  [7:0] LSByteBIn,
  input  [2:0] Inst,
  input  nCin,
  output Cn,
  output Zero,
  output Negative,
  output [7:0] MSbyte,
  output [7:0] LSByte
);

  wire alux8_1_cn, alux8_1_zero, n7400_1_pin2, n7400_1_pin3, n7400_1_pin11;

  ALUx8 alux8_1 (
    .Ain(LSByteAIn), .Bin(LSByteBIn), .Inst(Inst), .Cin(nCin), .Cn(alux8_1_cn), .Qout(LSByte),
    .Zero(alux8_1_zero));  // open: Pn
  _7400 #(.ShowInternalStructure("true")) u_7400_1 (
    .pin1(alux8_1_zero), .pin2(n7400_1_pin2), .pin3(n7400_1_pin3), .pin4(n7400_1_pin3), .pin5(n7400_1_pin3),
    .pin6(Zero), .pin13(alux8_1_cn), .pin12(alux8_1_cn), .pin11(n7400_1_pin11));  // open: pin10, pin9, pin8
  ALUx8 alux8_2 (
    .Ain(MSByteAIn), .Bin(MSByteBin), .Inst(Inst), .Cin(n7400_1_pin11), .Cn(Cn), .Qout(MSbyte),
    .Zero(n7400_1_pin2));  // open: Pn

  assign Negative = MSbyte[7];
endmodule

module ROMmanager (
  input  [14:0] AddressIn,
  output [7:0] MSByteOut,
  output [7:0] LSByteOut
);

  ROM #(.addrWidth(15)) rom_1 (.addr(AddressIn), .data(MSByteOut));
  ROM #(.addrWidth(15)) rom_2 (.addr(AddressIn), .data(LSByteOut));
endmodule
