// Logisim project TTLCopy.circ as structural Verilog: 2 circuits, main circuit main
module main (
  input  in_1,
  input  D0,
  input  in_3,
  input  in_4,
  input  in_5,
  input  RESET,
  input  prEnable,
  input  CLK,
  input  CI,
  input  UP,
  output Q0,
  output out_12,
  output out_13,
  output out_14,
  output CO
);

  wire and_1_out, and_2_out, and_3_out, and_4_out, and_5_out, and_6_out, and_7_out, d_ff_2_q, d_ff_2_qn,
       d_ff_3_q, d_ff_3_qn, d_ff_4_q, d_ff_4_qn, j_k_ff_1_q, j_k_ff_2_q, j_k_ff_2_qn, j_k_ff_3_q,
       j_k_ff_3_qn, j_k_ff_4_q, j_k_ff_4_qn, nand_1_out, nand_2_out, nand_3_out, nand_4_out, nand_5_out,
       nand_6_out, nand_7_out, nand_8_out, nand_9_out, nand_10_out, nand_11_out, nand_12_out, nand_13_out,
       nor_1_out, nor_2_out, not_1_out, not_2_out, not_4_out, not_5_out, not_6_out, not_7_out, not_8_out,
       not_9_out, not_11_out, not_12_out, not_14_out, not_15_out, not_17_out, not_18_out, not_20_out,
       or_1_out, or_2_out, undriven, xor_1_out, xor_2_out;

  D_Flip_Flop d_ff_1 (.D(undriven), .clk(in_1));  // open: Q, Qn, preset, reset
  _74161 #(.ShowInternalStructure("true")) u_74161_1 ();  // open: pin1, pin2, pin3, pin4, pin5, pin6, pin7, pin15, pin14, pin13, pin12, pin11, pin10, pin9
  or or_1 (or_1_out, d_ff_3_qn, d_ff_4_qn);
  not not_1 (not_1_out, CI);
  not not_2 (not_2_out, UP);
  and and_1 (and_1_out, d_ff_2_qn, d_ff_3_q);
  and and_2 (and_2_out, d_ff_2_q, or_1_out);
  nor nor_1 (nor_1_out, RESET, prEnable);
  nor nor_2 (nor_2_out, prEnable, RESET, CLK);
  not not_3 (CO, not_4_out);
  not not_4 (not_4_out, nand_1_out);
  nand nand_1 (nand_1_out, nand_2_out, xor_1_out, not_1_out);
  not not_5 (not_5_out, not_2_out);
  not not_6 (not_6_out, not_5_out);
  and and_3 (and_3_out, and_1_out, d_ff_4_q);
  not not_7 (not_7_out, RESET);
  not not_8 (not_8_out, nor_1_out);
  not not_9 (not_9_out, nor_2_out);
  xor xor_1 (xor_1_out, not_5_out, j_k_ff_1_q);
  D_Flip_Flop d_ff_2 (.D(or_2_out), .clk(in_1), .Q(d_ff_2_q), .Qn(d_ff_2_qn));  // open: preset, reset
  or or_2 (or_2_out, and_3_out, and_2_out);
  and and_4 (and_4_out, not_7_out, D0);
  J_K_Flip_Flop j_k_ff_1 (
    .J(not_8_out), .K(not_9_out), .clk(not_1_out), .Q(j_k_ff_1_q), .preset(and_4_out));  // open: Qn, reset
  nand nand_2 (nand_2_out, nand_3_out, nand_4_out);
  nand nand_3 (nand_3_out, not_5_out, j_k_ff_2_q, j_k_ff_3_q, j_k_ff_4_q);
  not not_10 (Q0, not_11_out);
  not not_11 (not_11_out, j_k_ff_1_q);
  nand nand_4 (nand_4_out, not_6_out, j_k_ff_2_qn, j_k_ff_3_qn, j_k_ff_4_qn);
  and and_5 (and_5_out, not_7_out, in_3);
  J_K_Flip_Flop j_k_ff_2 (
    .J(not_8_out), .K(not_9_out), .clk(not_12_out), .Q(j_k_ff_2_q), .Qn(j_k_ff_2_qn), .preset(and_5_out));  // open: reset
  not not_12 (not_12_out, nand_5_out);
  nand nand_5 (nand_5_out, not_1_out, xor_1_out);
  xor xor_2 (xor_2_out, d_ff_3_q, d_ff_4_q);
  not not_13 (out_12, not_14_out);
  not not_14 (not_14_out, j_k_ff_2_q);
  not not_15 (not_15_out, nand_6_out);
  nand nand_6 (nand_6_out, not_1_out, xor_1_out, nand_7_out);
  D_Flip_Flop d_ff_3 (.D(xor_2_out), .clk(in_1), .Q(d_ff_3_q), .Qn(d_ff_3_qn));  // open: preset, reset
  and and_6 (and_6_out, not_7_out, in_4);
  J_K_Flip_Flop j_k_ff_3 (
    .J(not_8_out), .K(not_9_out), .clk(not_15_out), .Q(j_k_ff_3_q), .Qn(j_k_ff_3_qn), .preset(and_6_out));  // open: reset
  nand nand_7 (nand_7_out, nand_8_out, nand_9_out);
  nand nand_8 (nand_8_out, not_5_out, j_k_ff_2_q);
  nand nand_9 (nand_9_out, not_6_out, j_k_ff_2_qn);
  not not_16 (out_13, not_17_out);
  not not_17 (not_17_out, j_k_ff_3_q);
  not not_18 (not_18_out, nand_10_out);
  nand nand_10 (nand_10_out, not_1_out, xor_1_out, nand_12_out);
  nand nand_11 (nand_11_out, not_5_out, j_k_ff_2_q, j_k_ff_3_q);
  and and_7 (and_7_out, not_7_out, in_5);
  J_K_Flip_Flop j_k_ff_4 (
    .J(not_8_out), .K(not_9_out), .clk(not_18_out), .Q(j_k_ff_4_q), .Qn(j_k_ff_4_qn), .preset(and_7_out));  // open: reset
  nand nand_12 (nand_12_out, nand_11_out, nand_13_out);
  nand nand_13 (nand_13_out, not_6_out, j_k_ff_2_qn, j_k_ff_3_qn);
  D_Flip_Flop d_ff_4 (.D(d_ff_4_qn), .clk(in_1), .Q(d_ff_4_q), .Qn(d_ff_4_qn));  // open: preset, reset
  not not_19 (out_14, not_20_out);
  not not_20 (not_20_out, j_k_ff_4_q);
endmodule

module x74161 (
  input  in_1,
  input  in_2,
  input  in_3,
  input  in_4,
  input  in_5,
  input  in_6,
  input  in_7,
  input  in_8,
  input  in_9
);

  wire and_1_out, and_2_out, and_3_out, and_4_out, and_5_out, and_6_out, and_7_out, and_8_out, buffer_1_out,
       buffer_2_out, buffer_3_out, buffer_4_out, buffer_5_out, buffer_6_out, nand_1_out, nor_2_out,
       nor_4_out, not_1_out, not_2_out, not_5_out, xor_1_out, xor_2_out, xor_3_out;

  buf buffer_1 (buffer_1_out, in_5);
  buf buffer_2 (buffer_2_out, in_6);
  not not_1 (not_1_out, in_7);
  not not_2 (not_2_out, not_1_out);
  // NOT_Gate not_3 has open pins: in=in_8, out=open
  // NOT_Gate not_4 has open pins: in=in_9, out=open
  nand nand_1 (nand_1_out, buffer_1_out, buffer_2_out);
  buf buffer_3 (buffer_3_out, in_1);
  not not_5 (not_5_out, nand_1_out);
  buf xor_1 (xor_1_out, not_5_out);  // XOR_Gate
  and and_1 (and_1_out, buffer_3_out, not_1_out);
  // NOR_Gate nor_1 has open pins: in0=and_1_out, in1=and_2_out, out=open
  and and_2 (and_2_out, xor_1_out, not_2_out);
  buf buffer_4 (buffer_4_out, in_2);
  // NOR_Gate nor_2 has open pins: out=nor_2_out
  and and_3 (and_3_out, buffer_4_out, not_1_out);
  // NOR_Gate nor_3 has open pins: in0=and_3_out, in1=and_4_out, out=open
  buf xor_2 (xor_2_out, nor_2_out);  // XOR_Gate
  and and_4 (and_4_out, xor_2_out, not_2_out);
  buf buffer_5 (buffer_5_out, in_3);
  and and_5 (and_5_out, buffer_5_out, not_1_out);
  // NOR_Gate nor_4 has open pins: out=nor_4_out
  buf xor_3 (xor_3_out, nor_4_out);  // XOR_Gate
  and and_6 (and_6_out, xor_3_out, not_2_out);
  // NOR_Gate nor_5 has open pins: in0=and_5_out, in1=and_6_out, out=open
  buf buffer_6 (buffer_6_out, in_4);
  buf and_7 (and_7_out, not_2_out);  // AND_Gate
  and and_8 (and_8_out, buffer_6_out, not_1_out);
  // NOR_Gate nor_6 has open pins: in0=and_8_out, in1=and_7_out, out=open
  D_Flip_Flop d_ff_1 ();  // open: D, clk, Q, Qn, preset, reset
  D_Flip_Flop d_ff_2 ();  // open: D, clk, Q, Qn, preset, reset
  D_Flip_Flop d_ff_3 ();  // open: D, clk, Q, Qn, preset, reset
  D_Flip_Flop d_ff_4 ();  // open: D, clk, Q, Qn, preset, reset
endmodule
