// Logisim project sdfghjkl.circ as structural Verilog: 2 circuits, main circuit main
module main (
  input  [15:0] in_1,
  output [7:0] out_2,
  output [7:0] out_3,
  output [7:0] out_4,
  output [7:0] out_5,
  output [7:0] out_6,
  output [7:0] out_7,
  output [7:0] out_8,
  output [7:0] out_9
);

  wire [7:0] rom_1_data, rom_3_data, rom_6_data, rom_7_data;

  ROM #(.addrWidth(15)) rom_1 (.addr(in_1[14:0]), .data(rom_1_data));
  ROM #(.addrWidth(15)) rom_2 (.addr(in_1[14:0]), .data(out_2));
  TwoxEightMux twoxeightmux_1 (.ByteA(out_2), .ByteB(rom_1_data), .byteSel(in_1[15]), .out_4(out_6));
  ROM #(.addrWidth(15)) rom_3 (.addr(in_1[14:0]), .data(rom_3_data));
  ROM #(.addrWidth(15)) rom_4 (.addr(in_1[14:0]), .data(out_3));
  TwoxEightMux twoxeightmux_2 (.ByteA(out_3), .ByteB(rom_3_data), .byteSel(in_1[15]), .out_4(out_7));
  ROM #(.addrWidth(15)) rom_5 (.addr(in_1[14:0]), .data(out_4));
  ROM #(.addrWidth(15)) rom_6 (.addr(in_1[14:0]), .data(rom_6_data));
  TwoxEightMux twoxeightmux_3 (.ByteA(out_4), .ByteB(rom_6_data), .byteSel(in_1[15]), .out_4(out_8));
  ROM #(.addrWidth(15)) rom_7 (.addr(in_1[14:0]), .data(rom_7_data));
  ROM #(.addrWidth(15)) rom_8 (.addr(in_1[14:0]), .data(out_5));
  TwoxEightMux twoxeightmux_4 (.ByteA(out_5), .ByteB(rom_7_data), .byteSel(in_1[15]), .out_4(out_9));

  // Notes on the sheet:
  //   contents of rom_1 (hex, n*v repeats v):
  //   16*0 ff fe fc f8 f0 e0 c0 80 8*0 40 80 15*0 ff fd f9 f1 e1 c1 81 1 1 1 2 4 8 10 20 80 16*0 ff fd f9
  //   f1 e1 c1 81 1 1 2 4 8 10 20 40 c0 80 15*0 ff fd f9 f1 e1 c1 81 1 2 3 6 c 18 30 60 17*0 ff fd f9 f1
  //   e1 c1 81 1 2 4 8 10 20 40 80 40 80 15*0 ff fd f9 f1 e1 c1 81 2 3 5 a 14 28 50 a0 80 16*0 ff fd f9 f1
  //   e1 c1 81 2 3 6 c 18 30 60 c0 c0 80 15*0 ff fd f9 f1 e1 c1 81 2 4 7 e 1c 38 70 e0 17*0 ff fd f9 f1 e1
  //   c1 81 2 4 8 10 20 40 80 0 40 80 15*0 ff fd f9 f1 e1 c1 82 3 5 9 12 24 48 90 20 80 16*0 ff fd f9 f1
  //   e1 c1 82 3 5 a 14 28 50 a0 40 c0 80 15*0 ff fd f9 f1 e1 c1 82 3 6 b 16 2c 58 b0 60 17*0 ff fd f9 f1
  //   e1 c1 82 3 6 c 18 30 60 c0 80 40 80 15*0 ff fd f9 f1 e1 c1 82 4 7 d 1a 34 68 d0 a0 80 16*0 ff fd f9
  //   f1 e1 c1 82 4 7 e 1c 38 70 e0 c0 c0 80 15*0 ff fd f9 f1 e1 c1 82 4 8 f 1e 3c 78 f0 e0 17*0 ff fd f9
  //   f1 e1 c1 82 4 8 10 20 40 80 0 0 40 80 15*0 ff fd f9 f1 e1 c2 83 5 9 11 22 44 88 10 20 80 16*0 ff fd
  //   f9 f1 e1 c2 83 5 9 12 24 48 90 20 40 c0 80 15*0 ff fd f9 f1 e1 c2 83 5 a 13 26 4c 98 30 60 17*0 ff
  //   fd f9 f1 e1 c2 83 5 a 14 28 50 a0 40 80 40 80 15*0 ff fd f9 f1 e1 c2 83 6 b 15 2a 54 a8 50 a0 80
  //   16*0 ff fd f9 f1 e1 c2 83 6 b 16 2c 58 b0 60 c0 c0 80 15*0 ff fd f9 f1 e1 c2 83 6 c 17 2e 5c b8 70
  //   e0 17*0 ff fd f9 f1 e1 c2 83 6 c 18 30 60 c0 80 0 40 80 15*0 ff fd f9 f1 e1 c2 84 7 d 19 32 64 c8 90
  //   20 80 16*0 ff fd f9 f1 e1 c2 84 7 d 1a 34 68 d0 a0 40 c0 80 15*0 ff fd f9 f1 e1 c2 84 7 e 1b 36 6c
  //   d8 b0 60 17*0 ff fd f9 f1 e1 c2 84 7 e 1c 38 70 e0 c0 80 40 80 15*0 ff fd f9 f1 e1 c2 84 8 f 1d 3a
  //   74 e8 d0 a0 80 16*0 ff fd f9 f1 e1 c2 84 8 f 1e 3c 78 f0 e0 c0 c0 80 15*0 ff fd f9 f1 e1 c2 84 8 10
  //   1f 3e 7c f8 f0 e0 17*0 ff fd f9 f1 e1 c2 84 8 10 20 40 80 0 0 0 40 80 15*0 ff fd f9 f1 e2 c3 85 9 11
  //   21 42 84 8 10 20 80 16*0 ff fd f9 f1 e2 c3 85 9 11 22 44 88 10 20 40 c0 80 15*0 ff fd f9 f1 e2 c3 85
  //   9 12 23 46 8c 18 30 60 17*0 ff fd f9 f1 e2 c3 85 9 12 24 48 90 20 40 80 40 80 15*0 ff fd f9 f1 e2 c3
  //   85 a 13 25 4a 94 28 50 a0 80 16*0 ff fd f9 f1 e2 c3 85 a 13 26 4c 98 30 60 c0 c0 80 15*0 ff fd f9 f1
  //   e2 c3 85 a 14 27 4e 9c 38 70 e0 17*0 ff fd f9 f1 e2 c3 85 a 14 28 50 a0 40 80 0 40 80 15*0 ff fd f9
  //   f1 e2 c3 86 b 15 29 52 a4 48 90 20 80 16*0 ff fd f9 f1 e2 c3 86 b 15 2a 54 a8 50 a0 40 c0 80 15*0 ff
  //   fd f9 f1 e2 c3 86 b 16 2b 56 ac 58 b0 60 17*0 ff fd f9 f1 e2 c3 86 b 16 2c 58 b0 60 c0 80 40 80 15*0
  //   ff fd f9 f1 e2 c3 86 c 17 2d 5a b4 68 d0 a0 80 16*0 ff fd f9 f1 e2 c3 86 c 17 2e 5c b8 70 e0 c0 c0
  //   80 15*0 ff fd f9 f1 e2 c3 86 c 18 2f 5e bc 78 f0 e0 17*0 ff fd f9 f1 e2 c3 86 c 18 30 60 c0 80 0 0
  //   40 80 15*0 ff fd f9 f1 e2 c4 87 d 19 31 62 c4 88 10 20 80 16*0 ff fd f9 f1 e2 c4 87 d 19 32 64 c8 90
  //   20 40 c0 80 15*0 ff fd f9 f1 e2 c4 87 d 1a 33 66 cc 98 30 60 17*0 ff fd f9 f1 e2 c4 87 d 1a 34 68 d0
  //   a0 40 80 40 80 15*0 ff fd f9 f1 e2 c4 87 e 1b 35 6a d4 a8 50 a0 80 16*0 ff fd f9 f1 e2 c4 87 e 1b 36
  //   6c d8 b0 60 c0 c0 80 15*0 ff fd f9 f1 e2 c4 87 e 1c 37 6e dc b8 70 e0 17*0 ff fd f9 f1 e2 c4 87 e 1c
  //   38 70 e0 c0 80 0 40 80 15*0 ff fd f9 f1 e2 c4 88 f 1d 39 72 e4 c8 90 20 80 16*0 ff fd f9 f1 e2 c4 88
  //   f 1d 3a 74 e8 d0 a0 40 c0 80 15*0 ff fd f9 f1 e2 c4 88 f 1e 3b 76 ec d8 b0 60 17*0 ff fd f9 f1 e2 c4
  //   88 f 1e 3c 78 f0 e0 c0 80 40 80 15*0 ff fd f9 f1 e2 c4 88 10 1f 3d 7a f4 e8 d0 a0 80 16*0 ff fd f9
  //   f1 e2 c4 88 10 1f 3e 7c f8 f0 e0 c0 c0 80 15*0 ff fd f9 f1 e2 c4 88 10 20 3f 7e fc f8 f0 e0 17*0 ff
  //   fd f9 f1 e2 c4 88 10 20 40 80 4*0 40 80 15*0 ff fd f9 f2 e3 c5 89 11 21 41 82 4 8 10 20 80 16*0 ff
  //   fd f9 f2 e3 c5 89 11 21 42 84 8 10 20 40 c0 80 15*0 ff fd f9 f2 e3 c5 89 11 22 43 86 c 18 30 60 17*0
  //   ff fd f9 f2 e3 c5 89 11 22 44 88 10 20 40 80 40 80 15*0 ff fd f9 f2 e3 c5 89 12 23 45 8a 14 28 50 a0
  //   80 16*0 ff fd f9 f2 e3 c5 89 12 23 46 8c 18 30 60 c0 c0 80 15*0 ff fd f9 f2 e3 c5 89 12 24 47 8e 1c
  //   38 70 e0 17*0 ff fd f9 f2 e3 c5 89 12 24 48 90 20 40 80 0 40 80 15*0 ff fd f9 f2 e3 c5 8a 13 25 49
  //   92 24 48 90 20 80 16*0 ff fd f9 f2 e3 c5 8a 13 25 4a 94 28 50 a0 40 c0 80 15*0 ff fd f9 f2 e3 c5 8a
  //   13 26 4b 96 2c 58 b0 60 17*0 ff fd f9 f2 e3 c5 8a 13 26 4c 98 30 60 c0 80 40 80 15*0 ff fd f9 f2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
  //   contents of rom_2 (hex, n*v repeats v):
  //   271*0 1 31*0 1 31*0 1 31*0 1 31*0 1 31*0 1 31*0 1 31*0 1 30*0 1 2 30*0 1 2 30*0 1 2 30*0 1 2 30*0 1
  //   2 30*0 1 2 30*0 1 2 30*0 1 2 30*0 1 3 30*0 1 3 30*0 1 3 30*0 1 3 30*0 1 3 30*0 1 3 30*0 1 3 30*0 1 3
  //   29*0 1 2 4 29*0 1 2 4 29*0 1 2 4 29*0 1 2 4 29*0 1 2 4 29*0 1 2 4 29*0 1 2 4 29*0 1 2 4 29*0 1 2 5
  //   29*0 1 2 5 29*0 1 2 5 29*0 1 2 5 29*0 1 2 5 29*0 1 2 5 29*0 1 2 5 29*0 1 2 5 29*0 1 3 6 29*0 1 3 6
  //   29*0 1 3 6 29*0 1 3 6 29*0 1 3 6 29*0 1 3 6 29*0 1 3 6 29*0 1 3 6 29*0 1 3 7 29*0 1 3 7 29*0 1 3 7
  //   29*0 1 3 7 29*0 1 3 7 29*0 1 3 7 29*0 1 3 7 29*0 1 3 7 28*0 1 2 4 8 28*0 1 2 4 8 28*0 1 2 4 8 28*0 1
  //   2 4 8 28*0 1 2 4 8 28*0 1 2 4 8 28*0 1 2 4 8 28*0 1 2 4 8 28*0 1 2 4 9 28*0 1 2 4 9 28*0 1 2 4 9
  //   28*0 1 2 4 9 28*0 1 2 4 9 28*0 1 2 4 9 28*0 1 2 4 9 28*0 1 2 4 9 28*0 1 2 5 a 28*0 1 2 5 a 28*0 1 2
  //   5 a 28*0 1 2 5 a 28*0 1 2 5 a 28*0 1 2 5 a 28*0 1 2 5 a 28*0 1 2 5 a 28*0 1 2 5 b 28*0 1 2 5 b 28*0
  //   1 2 5 b 28*0 1 2 5 b 28*0 1 2 5 b 28*0 1 2 5 b 28*0 1 2 5 b 28*0 1 2 5 b 28*0 1 3 6 c 28*0 1 3 6 c
  //   28*0 1 3 6 c 28*0 1 3 6 c 28*0 1 3 6 c 28*0 1 3 6 c 28*0 1 3 6 c 28*0 1 3 6 c 28*0 1 3 6 d 28*0 1 3
  //   6 d 28*0 1 3 6 d 28*0 1 3 6 d 28*0 1 3 6 d 28*0 1 3 6 d 28*0 1 3 6 d 28*0 1 3 6 d 28*0 1 3 7 e 28*0
  //   1 3 7 e 28*0 1 3 7 e 28*0 1 3 7 e 28*0 1 3 7 e 28*0 1 3 7 e 28*0 1 3 7 e 28*0 1 3 7 e 28*0 1 3 7 f
  //   28*0 1 3 7 f 28*0 1 3 7 f 28*0 1 3 7 f 28*0 1 3 7 f 28*0 1 3 7 f 28*0 1 3 7 f 28*0 1 3 7 f 27*0 1 2
  //   4 8 10 27*0 1 2 4 8 10 27*0 1 2 4 8 10 27*0 1 2 4 8 10 27*0 1 2 4 8 10 27*0 1 2 4 8 10 27*0 1 2 4 8
  //   10 27*0 1 2 4 8 10 27*0 1 2 4 8 11 27*0 1 2 4 8 11 27*0 1 2 4 8 11 27*0 1 2 4 8 11 27*0 1 2 4 8 11
  //   27*0 1 2 4 8 11 27*0 1 2 4 8 11 27*0 1 2 4 8 11 27*0 1 2 4 9 12 27*0 1 2 4 9 12 27*0 1 2 4 9 12 27*0
  //   1 2 4 9 12 27*0 1 2 4 9 12 27*0 1 2 4 9 12 27*0 1 2 4 9 12 27*0 1 2 4 9 12 27*0 1 2 4 9 13 27*0 1 2
  //   4 9 13 27*0 1 2 4 9 13 27*0 1 2 4 9 13 27*0 1 2 4 9 13 27*0 1 2 4 9 13 27*0 1 2 4 9 13 27*0 1 2 4 9
  //   13 27*0 1 2 5 a 14 27*0 1 2 5 a 14 27*0 1 2 5 a 14 27*0 1 2 5 a 14 27*0 1 2 5 a 14 27*0 1 2 5 a 14
  //   27*0 1 2 5 a 14 27*0 1 2 5 a 14 27*0 1 2 5 a 15 27*0 1 2 5 a 15 27*0 1 2 5 a 15 27*0 1 2 5 a 15 27*0
  //   1 2 5 a 15 27*0 1 2 5 a 15 27*0 1 2 5 a 15 27*0 1 2 5 a 15 27*0 1 2 5 b 16 27*0 1 2 5 b 16 27*0 1 2
  //   5 b 16 27*0 1 2 5 b 16 27*0 1 2 5 b 16 27*0 1 2 5 b 16 27*0 1 2 5 b 16 27*0 1 2 5 b 16 27*0 1 2 5 b
  //   17 27*0 1 2 5 b 17 27*0 1 2 5 b 17 27*0 1 2 5 b 17 27*0 1 2 5 b 17 27*0 1 2 5 b 17 27*0 1 2 5 b 17
  //   27*0 1 2 5 b 17 27*0 1 3 6 c 18 27*0 1 3 6 c 18 27*0 1 3 6 c 18 27*0 1 3 6 c 18 27*0 1 3 6 c 18 27*0
  //   1 3 6 c 18 27*0 1 3 6 c 18 27*0 1 3 6 c 18 27*0 1 3 6 c 19 27*0 1 3 6 c 19 27*0 1 3 6 c 19 27*0 1 3
  //   6 c 19 27*0 1 3 6 c 19 27*0 1 3 6 c 19 27*0 1 3 6 c 19 27*0 1 3 6 c 19 27*0 1 3 6 d 1a 27*0 1 3 6 d
  //   1a 27*0 1 3 6 d 1a 27*0 1 3 6 d 1a 27*0 1 3 6 d 1a 27*0 1 3 6 d 1a 27*0 1 3 6 d 1a 27*0 1 3 6 d 1a
  //   27*0 1 3 6 d 1b 27*0 1 3 6 d 1b 27*0 1 3 6 d 1b 27*0 1 3 6 d 1b 27*0 1 3 6 d 1b 27*0 1 3 6 d 1b 27*0
  //   1 3 6 d 1b 27*0 1 3 6 d 1b 27*0 1 3 7 e 1c 27*0 1 3 7 e 1c 27*0 1 3 7 e 1c 27*0 1 3 7 e 1c 27*0 1 3
  //   7 e 1c 27*0 1 3 7 e 1c 27*0 1 3 7 e 1c 27*0 1 3 7 e 1c 27*0 1 3 7 e 1d 27*0 1 3 7 e 1d 27*0 1 3 7 e
  //   1d 27*0 1 3 7 e 1d 27*0 1 3 7 e 1d 27*0 1 3 7 e 1d 27*0 1 3 7 e 1d 27*0 1 3 7 e 1d 27*0 1 3 7 f 1e
  //   27*0 1 3 7 f 1e 27*0 1 3 7 f 1e 27*0 1 3 7 f 1e 27*0 1 3 7 f 1e 27*0 1 3 7 f 1e 27*0 1 3 7 f 1e 27*0
  //   1 3 7 f 1e 27*0 1 3 7 f 1f 27*0 1 3 7 f 1f 27*0 1 3 7 f 1f 27*0 1 3 7 f 1f 27*0 1 3 7 f 1f 27*0 1 3
  //   7 f 1f 27*0 1 3 7 f 1f 27*0 1 3 7 f 1f 26*0 1 2 4 8 10 20 26*0 1 2 4 8 10 20 26*0 1 2 4 8 10 20 26*0
  //   1 2 4 8 10 20 26*0 1 2 4 8 10 20 26*0 1 2 4 8 10 20 26*0 1 2 4 8 10 20 26*0 1 2 4 8 10 20 26*0 1 2 4
  //   8 10 21 26*0 1 2 4 8 10 21 26*0 1 2 4 8 10 21 26*0 1 2 4 8 10 21 26*0 1 2 4 8 10 21 26*0 1 2 4 8 10
  //   21 26*0 1 2 4 8 10 21 26*0 1 2 4 8 10 21 26*0 1 2 4 8 11 22 26*0 1 2 4 8 11 22 26*0 1 2 4 8 11 22
  //   26*0 1 2 4 8 11 22 26*0 1 2 4 8 11 22 26*0 1 2 4 8 11 22 26*0 1 2 4 8 11 22 26*0 1 2 4 8 11 22 26*0
  //   1 2 4 8 11 23 26*0 1 2 4 8 11 23 26*0 1 2 4 8 11 23 26*0 1 2 4 8 11 23 26*0 1 2 4 8 11 23 26*0 1 2 4
  //   8 11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
  //   contents of rom_3 (hex, n*v repeats v):
  //   16*0 9*ff fe fc f8 f0 e0 c0 80 0 0 1 2 4 8 10 20 40 80 7*0 8*ff fe fc f8 f0 e0 c0 80 0 1 2 4 8 10 20
  //   40 80 8*0 8*ff fe fc f8 f0 e0 c0 80 0 1 3 6 c 18 30 60 c0 80 7*0 8*ff fe fc f8 f0 e0 c0 80 1 2 4 8
  //   10 20 40 80 9*0 8*ff fe fc f8 f0 e0 c0 80 1 2 5 a 14 28 50 a0 40 80 7*0 8*ff fe fc f8 f0 e0 c0 80 1
  //   3 6 c 18 30 60 c0 80 8*0 8*ff fe fc f8 f0 e0 c0 80 1 3 7 e 1c 38 70 e0 c0 80 7*0 8*ff fe fc f8 f0 e0
  //   c0 80 2 4 8 10 20 40 80 10*0 8*ff fe fc f8 f0 e0 c0 81 2 4 9 12 24 48 90 20 40 80 7*0 8*ff fe fc f8
  //   f0 e0 c0 81 2 5 a 14 28 50 a0 40 80 8*0 8*ff fe fc f8 f0 e0 c0 81 2 5 b 16 2c 58 b0 60 c0 80 7*0
  //   8*ff fe fc f8 f0 e0 c0 81 3 6 c 18 30 60 c0 80 9*0 8*ff fe fc f8 f0 e0 c0 81 3 6 d 1a 34 68 d0 a0 40
  //   80 7*0 8*ff fe fc f8 f0 e0 c0 81 3 7 e 1c 38 70 e0 c0 80 8*0 8*ff fe fc f8 f0 e0 c0 81 3 7 f 1e 3c
  //   78 f0 e0 c0 80 7*0 8*ff fe fc f8 f0 e0 c0 81 4 8 10 20 40 80 11*0 8*ff fe fc f8 f0 e0 c1 82 4 8 11
  //   22 44 88 10 20 40 80 7*0 8*ff fe fc f8 f0 e0 c1 82 4 9 12 24 48 90 20 40 80 8*0 8*ff fe fc f8 f0 e0
  //   c1 82 4 9 13 26 4c 98 30 60 c0 80 7*0 8*ff fe fc f8 f0 e0 c1 82 5 a 14 28 50 a0 40 80 9*0 8*ff fe fc
  //   f8 f0 e0 c1 82 5 a 15 2a 54 a8 50 a0 40 80 7*0 8*ff fe fc f8 f0 e0 c1 82 5 b 16 2c 58 b0 60 c0 80
  //   8*0 8*ff fe fc f8 f0 e0 c1 82 5 b 17 2e 5c b8 70 e0 c0 80 7*0 8*ff fe fc f8 f0 e0 c1 82 6 c 18 30 60
  //   c0 80 10*0 8*ff fe fc f8 f0 e0 c1 83 6 c 19 32 64 c8 90 20 40 80 7*0 8*ff fe fc f8 f0 e0 c1 83 6 d
  //   1a 34 68 d0 a0 40 80 8*0 8*ff fe fc f8 f0 e0 c1 83 6 d 1b 36 6c d8 b0 60 c0 80 7*0 8*ff fe fc f8 f0
  //   e0 c1 83 7 e 1c 38 70 e0 c0 80 9*0 8*ff fe fc f8 f0 e0 c1 83 7 e 1d 3a 74 e8 d0 a0 40 80 7*0 8*ff fe
  //   fc f8 f0 e0 c1 83 7 f 1e 3c 78 f0 e0 c0 80 8*0 8*ff fe fc f8 f0 e0 c1 83 7 f 1f 3e 7c f8 f0 e0 c0 80
  //   7*0 8*ff fe fc f8 f0 e0 c1 83 8 10 20 40 80 12*0 8*ff fe fc f8 f0 e1 c2 84 8 10 21 42 84 8 10 20 40
  //   80 7*0 8*ff fe fc f8 f0 e1 c2 84 8 11 22 44 88 10 20 40 80 8*0 8*ff fe fc f8 f0 e1 c2 84 8 11 23 46
  //   8c 18 30 60 c0 80 7*0 8*ff fe fc f8 f0 e1 c2 84 9 12 24 48 90 20 40 80 9*0 8*ff fe fc f8 f0 e1 c2 84
  //   9 12 25 4a 94 28 50 a0 40 80 7*0 8*ff fe fc f8 f0 e1 c2 84 9 13 26 4c 98 30 60 c0 80 8*0 8*ff fe fc
  //   f8 f0 e1 c2 84 9 13 27 4e 9c 38 70 e0 c0 80 7*0 8*ff fe fc f8 f0 e1 c2 84 a 14 28 50 a0 40 80 10*0
  //   8*ff fe fc f8 f0 e1 c2 85 a 14 29 52 a4 48 90 20 40 80 7*0 8*ff fe fc f8 f0 e1 c2 85 a 15 2a 54 a8
  //   50 a0 40 80 8*0 8*ff fe fc f8 f0 e1 c2 85 a 15 2b 56 ac 58 b0 60 c0 80 7*0 8*ff fe fc f8 f0 e1 c2 85
  //   b 16 2c 58 b0 60 c0 80 9*0 8*ff fe fc f8 f0 e1 c2 85 b 16 2d 5a b4 68 d0 a0 40 80 7*0 8*ff fe fc f8
  //   f0 e1 c2 85 b 17 2e 5c b8 70 e0 c0 80 8*0 8*ff fe fc f8 f0 e1 c2 85 b 17 2f 5e bc 78 f0 e0 c0 80 7*0
  //   8*ff fe fc f8 f0 e1 c2 85 c 18 30 60 c0 80 11*0 8*ff fe fc f8 f0 e1 c3 86 c 18 31 62 c4 88 10 20 40
  //   80 7*0 8*ff fe fc f8 f0 e1 c3 86 c 19 32 64 c8 90 20 40 80 8*0 8*ff fe fc f8 f0 e1 c3 86 c 19 33 66
  //   cc 98 30 60 c0 80 7*0 8*ff fe fc f8 f0 e1 c3 86 d 1a 34 68 d0 a0 40 80 9*0 8*ff fe fc f8 f0 e1 c3 86
  //   d 1a 35 6a d4 a8 50 a0 40 80 7*0 8*ff fe fc f8 f0 e1 c3 86 d 1b 36 6c d8 b0 60 c0 80 8*0 8*ff fe fc
  //   f8 f0 e1 c3 86 d 1b 37 6e dc b8 70 e0 c0 80 7*0 8*ff fe fc f8 f0 e1 c3 86 e 1c 38 70 e0 c0 80 10*0
  //   8*ff fe fc f8 f0 e1 c3 87 e 1c 39 72 e4 c8 90 20 40 80 7*0 8*ff fe fc f8 f0 e1 c3 87 e 1d 3a 74 e8
  //   d0 a0 40 80 8*0 8*ff fe fc f8 f0 e1 c3 87 e 1d 3b 76 ec d8 b0 60 c0 80 7*0 8*ff fe fc f8 f0 e1 c3 87
  //   f 1e 3c 78 f0 e0 c0 80 9*0 8*ff fe fc f8 f0 e1 c3 87 f 1e 3d 7a f4 e8 d0 a0 40 80 7*0 8*ff fe fc f8
  //   f0 e1 c3 87 f 1f 3e 7c f8 f0 e0 c0 80 8*0 8*ff fe fc f8 f0 e1 c3 87 f 1f 3f 7e fc f8 f0 e0 c0 80 7*0
  //   8*ff fe fc f8 f0 e1 c3 87 10 20 40 80 13*0 8*ff fe fc f8 f1 e2 c4 88 10 20 41 82 4 8 10 20 40 80 7*0
  //   8*ff fe fc f8 f1 e2 c4 88 10 21 42 84 8 10 20 40 80 8*0 8*ff fe fc f8 f1 e2 c4 88 10 21 43 86 c 18
  //   30 60 c0 80 7*0 8*ff fe fc f8 f1 e2 c4 88 11 22 44 88 10 20 40 80 9*0 8*ff fe fc f8 f1 e2 c4 88 11
  //   22 45 8a 14 28 50 a0 40 80 7*0 8*ff fe fc f8 f1 e2 c4 88 11 23 46 8c 18 30 60 c0 80 8*0 8*ff fe fc
  //   f8 f1 e2 c4 88 11 23 47 8e 1c 38 70 e0 c0 80 7*0 8*ff fe fc f8 f1 e2 c4 88 12 24 48 90 20 40 80 10*0
  //   8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
  //   contents of rom_4 (hex, n*v repeats v):
  //   42*0 1 2 4 8 10 20 25*0 1 2 4 8 10 20 40 25*0 1 3 6 c 18 30 60 24*0 1 2 4 8 10 20 40 80 24*0 1 2 5 a
  //   14 28 50 a0 24*0 1 3 6 c 18 30 60 c0 24*0 1 3 7 e 1c 38 70 e0 23*0 1 2 4 8 10 20 40 80 24*0 1 2 4 9
  //   12 24 48 90 20 23*0 1 2 5 a 14 28 50 a0 40 23*0 1 2 5 b 16 2c 58 b0 60 23*0 1 3 6 c 18 30 60 c0 80
  //   23*0 1 3 6 d 1a 34 68 d0 a0 23*0 1 3 7 e 1c 38 70 e0 c0 23*0 1 3 7 f 1e 3c 78 f0 e0 22*0 1 2 4 8 10
  //   20 40 80 24*0 1 2 4 8 11 22 44 88 10 20 22*0 1 2 4 9 12 24 48 90 20 40 22*0 1 2 4 9 13 26 4c 98 30
  //   60 22*0 1 2 5 a 14 28 50 a0 40 80 22*0 1 2 5 a 15 2a 54 a8 50 a0 22*0 1 2 5 b 16 2c 58 b0 60 c0 22*0
  //   1 2 5 b 17 2e 5c b8 70 e0 22*0 1 3 6 c 18 30 60 c0 80 23*0 1 3 6 c 19 32 64 c8 90 20 22*0 1 3 6 d 1a
  //   34 68 d0 a0 40 22*0 1 3 6 d 1b 36 6c d8 b0 60 22*0 1 3 7 e 1c 38 70 e0 c0 80 22*0 1 3 7 e 1d 3a 74
  //   e8 d0 a0 22*0 1 3 7 f 1e 3c 78 f0 e0 c0 22*0 1 3 7 f 1f 3e 7c f8 f0 e0 21*0 1 2 4 8 10 20 40 80 24*0
  //   1 2 4 8 10 21 42 84 8 10 20 21*0 1 2 4 8 11 22 44 88 10 20 40 21*0 1 2 4 8 11 23 46 8c 18 30 60 21*0
  //   1 2 4 9 12 24 48 90 20 40 80 21*0 1 2 4 9 12 25 4a 94 28 50 a0 21*0 1 2 4 9 13 26 4c 98 30 60 c0
  //   21*0 1 2 4 9 13 27 4e 9c 38 70 e0 21*0 1 2 5 a 14 28 50 a0 40 80 22*0 1 2 5 a 14 29 52 a4 48 90 20
  //   21*0 1 2 5 a 15 2a 54 a8 50 a0 40 21*0 1 2 5 a 15 2b 56 ac 58 b0 60 21*0 1 2 5 b 16 2c 58 b0 60 c0
  //   80 21*0 1 2 5 b 16 2d 5a b4 68 d0 a0 21*0 1 2 5 b 17 2e 5c b8 70 e0 c0 21*0 1 2 5 b 17 2f 5e bc 78
  //   f0 e0 21*0 1 3 6 c 18 30 60 c0 80 23*0 1 3 6 c 18 31 62 c4 88 10 20 21*0 1 3 6 c 19 32 64 c8 90 20
  //   40 21*0 1 3 6 c 19 33 66 cc 98 30 60 21*0 1 3 6 d 1a 34 68 d0 a0 40 80 21*0 1 3 6 d 1a 35 6a d4 a8
  //   50 a0 21*0 1 3 6 d 1b 36 6c d8 b0 60 c0 21*0 1 3 6 d 1b 37 6e dc b8 70 e0 21*0 1 3 7 e 1c 38 70 e0
  //   c0 80 22*0 1 3 7 e 1c 39 72 e4 c8 90 20 21*0 1 3 7 e 1d 3a 74 e8 d0 a0 40 21*0 1 3 7 e 1d 3b 76 ec
  //   d8 b0 60 21*0 1 3 7 f 1e 3c 78 f0 e0 c0 80 21*0 1 3 7 f 1e 3d 7a f4 e8 d0 a0 21*0 1 3 7 f 1f 3e 7c
  //   f8 f0 e0 c0 21*0 1 3 7 f 1f 3f 7e fc f8 f0 e0 20*0 1 2 4 8 10 20 40 80 24*0 1 2 4 8 10 20 41 82 4 8
  //   10 20 20*0 1 2 4 8 10 21 42 84 8 10 20 40 20*0 1 2 4 8 10 21 43 86 c 18 30 60 20*0 1 2 4 8 11 22 44
  //   88 10 20 40 80 20*0 1 2 4 8 11 22 45 8a 14 28 50 a0 20*0 1 2 4 8 11 23 46 8c 18 30 60 c0 20*0 1 2 4
  //   8 11 23 47 8e 1c 38 70 e0 20*0 1 2 4 9 12 24 48 90 20 40 80 21*0 1 2 4 9 12 24 49 92 24 48 90 20
  //   20*0 1 2 4 9 12 25 4a 94 28 50 a0 40 20*0 1 2 4 9 12 25 4b 96 2c 58 b0 60 20*0 1 2 4 9 13 26 4c 98
  //   30 60 c0 80 20*0 1 2 4 9 13 26 4d 9a 34 68 d0 a0 20*0 1 2 4 9 13 27 4e 9c 38 70 e0 c0 20*0 1 2 4 9
  //   13 27 4f 9e 3c 78 f0 e0 20*0 1 2 5 a 14 28 50 a0 40 80 22*0 1 2 5 a 14 28 51 a2 44 88 10 20 20*0 1 2
  //   5 a 14 29 52 a4 48 90 20 40 20*0 1 2 5 a 14 29 53 a6 4c 98 30 60 20*0 1 2 5 a 15 2a 54 a8 50 a0 40
  //   80 20*0 1 2 5 a 15 2a 55 aa 54 a8 50 a0 20*0 1 2 5 a 15 2b 56 ac 58 b0 60 c0 20*0 1 2 5 a 15 2b 57
  //   ae 5c b8 70 e0 20*0 1 2 5 b 16 2c 58 b0 60 c0 80 21*0 1 2 5 b 16 2c 59 b2 64 c8 90 20 20*0 1 2 5 b
  //   16 2d 5a b4 68 d0 a0 40 20*0 1 2 5 b 16 2d 5b b6 6c d8 b0 60 20*0 1 2 5 b 17 2e 5c b8 70 e0 c0 80
  //   20*0 1 2 5 b 17 2e 5d ba 74 e8 d0 a0 20*0 1 2 5 b 17 2f 5e bc 78 f0 e0 c0 20*0 1 2 5 b 17 2f 5f be
  //   7c f8 f0 e0 20*0 1 3 6 c 18 30 60 c0 80 23*0 1 3 6 c 18 30 61 c2 84 8 10 20 20*0 1 3 6 c 18 31 62 c4
  //   88 10 20 40 20*0 1 3 6 c 18 31 63 c6 8c 18 30 60 20*0 1 3 6 c 19 32 64 c8 90 20 40 80 20*0 1 3 6 c
  //   19 32 65 ca 94 28 50 a0 20*0 1 3 6 c 19 33 66 cc 98 30 60 c0 20*0 1 3 6 c 19 33 67 ce 9c 38 70 e0
  //   20*0 1 3 6 d 1a 34 68 d0 a0 40 80 21*0 1 3 6 d 1a 34 69 d2 a4 48 90 20 20*0 1 3 6 d 1a 35 6a d4 a8
  //   50 a0 40 20*0 1 3 6 d 1a 35 6b d6 ac 58 b0 60 20*0 1 3 6 d 1b 36 6c d8 b0 60 c0 80 20*0 1 3 6 d 1b
  //   36 6d da b4 68 d0 a0 20*0 1 3 6 d 1b 37 6e dc b8 70 e0 c0 20*0 1 3 6 d 1b 37 6f de bc 78 f0 e0 20*0
  //   1 3 7 e 1c 38 70 e0 c0 80 22*0 1 3 7 e 1c 38 71 e2 c4 88 10 20 20*0 1 3 7 e 1c 39 72 e4 c8 90 20 40
  //   20*0 1 3 7 e 1c 39 73 e6 cc 98 30 60 20*0 1 3 7 e 1d 3a 74 e8 d0 a0 40 80 20*0 1 3 7 e 1d 3a 75 ea
  //   d4 a8 50 a0 20*0 1 3 7 e 1d 3b 76 ec d8 b0 60 c0 20*0 1 3 7 e 1d 3b 77 ee dc b8 70 e0 20*0 1 3 7 f
  //   1e 3c 78 f0 e0 c0 80 21*0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
  //   contents of rom_5 (hex, n*v repeats v):
  //   34*0 1 2 4 8 10 20 40 80 23*0 1 2 4 8 10 20 40 80 24*0 1 3 6 c 18 30 60 c0 80 22*0 1 2 4 8 10 20 40
  //   80 24*0 1 2 5 a 14 28 50 a0 40 80 22*0 1 3 6 c 18 30 60 c0 80 23*0 1 3 7 e 1c 38 70 e0 c0 80 22*0 2
  //   4 8 10 20 40 80 24*0 1 2 4 9 12 24 48 90 20 40 80 21*0 1 2 5 a 14 28 50 a0 40 80 22*0 1 2 5 b 16 2c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
  //   contents of rom_6 (hex, n*v repeats v):
  //   ff fe fc f8 f0 e0 c0 80 8*0 17*ff fe fc f8 f0 e0 c0 80 0 0 1 2 4 8 10 20 0 16*ff fe fc f8 f0 e0 c0
  //   80 0 1 2 4 8 10 20 40 0 16*ff fe fc f8 f0 e0 c0 80 0 1 3 6 c 18 30 60 0 16*ff fe fc f8 f0 e0 c0 80 1
  //   2 4 8 10 20 40 80 0 16*ff fe fc f8 f0 e0 c0 80 1 2 5 a 14 28 50 a0 0 16*ff fe fc f8 f0 e0 c0 80 1 3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
  //   contents of rom_7 (hex, n*v repeats v):
  //   46 46 20 46 46 20 46 46 20 46 46 20 46 46 20 46 46 20 46 46 20 46 46 20 46 46 20 46 45 20 46 43 20
  //   46 38 20 46 30 20 45 30 20 43 30 20 38 30 d a 46 46 20 46 46 20 46 46 20 46 46 20 46 46 20 46 46 20
  //   46 46 20 46 46 20 46 46 20 46 46 20 46 46 20 46 46 20 46 46 20 46 46 20 46 46 20 46 46 d a 46 46 20
  //   4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
  //   contents of rom_8 (hex, n*v repeats v):
  //   32*0 40 80 24*0 1 2 4 8 10 20 80 24*0 1 2 4 8 10 20 40 c0 80 23*0 1 3 6 c 18 30 60 24*0 1 2 4 8 10
  //   20 40 80 40 80 22*0 1 2 5 a 14 28 50 a0 80 23*0 1 3 6 c 18 30 60 c0 c0 80 22*0 1 3 7 e 1c 38 70 e0
  //   23*0 1 2 4 8 10 20 40 80 0 40 80 21*0 1 2 4 9 12 24 48 90 20 80 22*0 1 2 5 a 14 28 50 a0 40 c0 80
  //   21*0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
endmodule

module TwoxEightMux (
  input  [7:0] ByteA,
  input  [7:0] ByteB,
  input  byteSel,
  output [7:0] out_4
);

  wire n74157_1_pin15, n74157_2_pin15;

  _74157 #(.ShowInternalStructure("true")) u_74157_1 (
    .pin1(byteSel), .pin2(ByteA[4]), .pin3(ByteB[4]), .pin4(out_4[4]), .pin5(ByteA[5]), .pin6(ByteB[5]),
    .pin7(out_4[5]), .pin15(n74157_1_pin15), .pin14(ByteA[7]), .pin13(ByteB[7]), .pin12(out_4[7]),
    .pin11(ByteA[6]), .pin10(ByteB[6]), .pin9(out_4[6]));
  _74157 #(.ShowInternalStructure("true")) u_74157_2 (
    .pin1(byteSel), .pin2(ByteA[0]), .pin3(ByteB[0]), .pin4(out_4[0]), .pin5(ByteA[1]), .pin6(ByteB[1]),
    .pin7(out_4[1]), .pin15(n74157_2_pin15), .pin14(ByteA[3]), .pin13(ByteB[3]), .pin12(out_4[3]),
    .pin11(ByteA[2]), .pin10(ByteB[2]), .pin9(out_4[2]));
  // also tied to GND on the sheet: {n74157_1_pin15, n74157_2_pin15}
endmodule
